// Logisim project F3.2_F3.3.circ as structural Verilog: 1 circuit, main circuit workplace_F3_2_F3_3
module workplace_F3_2_F3_3 (
  input  in_1,
  input  in_2,
  input  in_3,
  input  in_4,
  input  in_5,
  input  in_6,
  input  in_7,
  input  in_8,
  input  in_9,
  input  in_10,
  input  in_11,
  output out_12,
  output out_13,
  output out_14,
  output out_15,
  output out_16
);

  wire transistor_1_out, transistor_3_out, transistor_5_out, transistor_8_out, transistor_9_out,
       transistor_11_out, transistor_13_out, transistor_17_out, transistor_19_out, transistor_23_out,
       transistor_25_out, transistor_27_out, transistor_28_out, transistor_30_out, transistor_34_out,
       transistor_37_out, transistor_40_out, transistor_41_out, transistor_44_out, transistor_48_out,
       transistor_49_out, transistor_52_out;

  Transistor transistor_1 (.in(1'b1), .out(transistor_1_out), .gate(in_8));
  Transistor #(.\type ("n")) transistor_2 (.in(1'b0), .out(transistor_1_out), .gate(in_8));
  Transistor transistor_3 (.in(1'b1), .out(transistor_3_out), .gate(in_10));
  Transistor #(.\type ("n")) transistor_4 (.in(1'b0), .out(transistor_3_out), .gate(in_10));
  Transistor transistor_5 (.in(1'b1), .out(transistor_5_out), .gate(in_1));
  Transistor transistor_6 (.in(transistor_5_out), .out(out_12), .gate(in_2));
  Transistor #(.\type ("n")) transistor_7 (.in(1'b0), .out(out_12), .gate(in_1));
  Transistor transistor_8 (.in(1'b1), .out(transistor_8_out), .gate(in_3));
  Transistor transistor_9 (.in(transistor_8_out), .out(transistor_9_out), .gate(in_4));
  Transistor #(.\type ("n")) transistor_10 (.in(1'b0), .out(transistor_9_out), .gate(in_3));
  Transistor transistor_11 (.in(1'b1), .out(transistor_11_out), .gate(in_5));
  Transistor #(.\type ("n")) transistor_12 (.in(transistor_13_out), .out(transistor_11_out), .gate(in_5));
  Transistor #(.\type ("n")) transistor_13 (.in(1'b0), .out(transistor_13_out), .gate(in_6));
  Transistor #(.\type ("n")) transistor_14 (.in(1'b0), .out(out_12), .gate(in_2));
  Transistor #(.\type ("n")) transistor_15 (.in(1'b0), .out(transistor_9_out), .gate(in_4));
  Transistor transistor_16 (.in(1'b1), .out(transistor_11_out), .gate(in_6));
  Transistor transistor_17 (.in(1'b1), .out(transistor_17_out), .gate(in_9));
  Transistor #(.\type ("n")) transistor_18 (.in(1'b0), .out(transistor_17_out), .gate(in_9));
  Transistor transistor_19 (.in(1'b1), .out(transistor_19_out), .gate(in_11));
  Transistor #(.\type ("n")) transistor_20 (.in(1'b0), .out(transistor_19_out), .gate(in_11));
  Transistor transistor_21 (.in(1'b1), .out(out_13), .gate(transistor_9_out));
  Transistor #(.\type ("n")) transistor_22 (.in(1'b0), .out(out_13), .gate(transistor_9_out));
  Transistor transistor_23 (.in(1'b1), .out(transistor_23_out), .gate(transistor_11_out));
  Transistor #(.\type ("n")) transistor_24 (.in(1'b0), .out(transistor_23_out), .gate(transistor_11_out));
  Transistor transistor_25 (.in(1'b1), .out(transistor_25_out), .gate(transistor_1_out));
  Transistor #(.\type ("n")) transistor_26 (.in(transistor_27_out), .out(transistor_25_out), .gate(transistor_1_out));
  Transistor #(.\type ("n")) transistor_27 (.in(1'b0), .out(transistor_27_out), .gate(in_9));
  Transistor transistor_28 (.in(1'b1), .out(transistor_28_out), .gate(transistor_3_out));
  Transistor #(.\type ("n")) transistor_29 (.in(transistor_30_out), .out(transistor_28_out), .gate(transistor_3_out));
  Transistor #(.\type ("n")) transistor_30 (.in(1'b0), .out(transistor_30_out), .gate(in_11));
  Transistor transistor_31 (.in(1'b1), .out(out_14), .gate(transistor_23_out));
  Transistor transistor_32 (.in(1'b1), .out(out_14), .gate(in_7));
  Transistor #(.\type ("n")) transistor_33 (.in(transistor_34_out), .out(out_14), .gate(transistor_23_out));
  Transistor #(.\type ("n")) transistor_34 (.in(1'b0), .out(transistor_34_out), .gate(in_7));
  Transistor transistor_35 (.in(1'b1), .out(transistor_25_out), .gate(in_9));
  Transistor transistor_36 (.in(1'b1), .out(transistor_28_out), .gate(in_11));
  Transistor transistor_37 (.in(1'b1), .out(transistor_37_out), .gate(transistor_17_out));
  Transistor transistor_38 (.in(1'b1), .out(transistor_37_out), .gate(in_8));
  Transistor #(.\type ("n")) transistor_39 (.in(transistor_40_out), .out(transistor_37_out), .gate(transistor_17_out));
  Transistor #(.\type ("n")) transistor_40 (.in(1'b0), .out(transistor_40_out), .gate(in_8));
  Transistor transistor_41 (.in(1'b1), .out(transistor_41_out), .gate(transistor_19_out));
  Transistor transistor_42 (.in(1'b1), .out(transistor_41_out), .gate(in_10));
  Transistor #(.\type ("n")) transistor_43 (.in(transistor_44_out), .out(transistor_41_out), .gate(transistor_19_out));
  Transistor #(.\type ("n")) transistor_44 (.in(1'b0), .out(transistor_44_out), .gate(in_10));
  Transistor transistor_45 (.in(1'b1), .out(out_15), .gate(transistor_25_out));
  Transistor transistor_46 (.in(1'b1), .out(out_15), .gate(transistor_37_out));
  Transistor #(.\type ("n")) transistor_47 (.in(transistor_48_out), .out(out_15), .gate(transistor_25_out));
  Transistor #(.\type ("n")) transistor_48 (.in(1'b0), .out(transistor_48_out), .gate(transistor_37_out));
  Transistor transistor_49 (.in(1'b1), .out(transistor_49_out), .gate(transistor_28_out));
  Transistor transistor_50 (.in(1'b1), .out(transistor_49_out), .gate(transistor_41_out));
  Transistor #(.\type ("n")) transistor_51 (.in(transistor_52_out), .out(transistor_49_out), .gate(transistor_28_out));
  Transistor #(.\type ("n")) transistor_52 (.in(1'b0), .out(transistor_52_out), .gate(transistor_41_out));
  Transistor transistor_53 (.in(1'b1), .out(out_16), .gate(transistor_49_out));
  Transistor #(.\type ("n")) transistor_54 (.in(1'b0), .out(out_16), .gate(transistor_49_out));

  // Notes on the sheet:
  //   NOR
  //   OR
  //   3-input NAND (10 transistors)
  //   XOR (16 transistors)
  //   XNOR (18 transistors)
endmodule
