// Logisim project F3.5.circ as structural Verilog: 20 circuits, main circuit S_R_latch
module workplace_F3_5 (
  input  in_1,
  input  [3:0] in_2,
  input  in_3,
  input  R,
  input  EN,
  input  [3:0] max,
  input  [3:0] in_7,
  input  [3:0] in_8,
  input  in_9,
  output [3:0] Q,
  output C,
  output [3:0] out_12,
  output [7:0] out_13
);

  wire and_1_out, and_2_out, button_1_out, button_2_out, button_3_out, button_4_out, button_5_out,
       button_6_out, button_7_out, button_8_out, clk_out, clock_1_out, clock_2_out, clock_3_out, clock_4_out,
       clock_5_out, clock_6_out, clock_7_out, counter_2_16_tunable_1_c, counter_2_16_tunable_2_c,
       counter_2_16_tunable_3_c, counter_2_16_tunable_5_c, counter_2_16_tunable_6_c, d_flip_flop_r_1_q,
       d_flip_flop_r_en_1_q, d_flip_flop_r_en_2_q, d_flip_flop_r_en_3_q, d_flip_flop_r_en_4_q,
       d_flip_flop_r_en_5_q, d_flip_flop_r_en_6_q, d_flip_flop_r_en_7_q, d_flip_flop_r_negedge_1_q,
       decoder_7_segments_1_sa, decoder_7_segments_1_sb, decoder_7_segments_1_sc, decoder_7_segments_1_sd,
       decoder_7_segments_1_se, decoder_7_segments_1_sf, decoder_7_segments_1_sg, decoder_7_segments_1_sh,
       decoder_7_segments_2_sa, decoder_7_segments_2_sb, decoder_7_segments_2_sc, decoder_7_segments_2_sd,
       decoder_7_segments_2_se, decoder_7_segments_2_sf, decoder_7_segments_2_sg, decoder_7_segments_2_sh,
       decoder_7_segments_3_sa, decoder_7_segments_3_sb, decoder_7_segments_3_sc, decoder_7_segments_3_sd,
       decoder_7_segments_3_se, decoder_7_segments_3_sf, decoder_7_segments_3_sg, decoder_7_segments_3_sh,
       decoder_7_segments_4_sa, decoder_7_segments_4_sb, decoder_7_segments_4_sc, decoder_7_segments_4_sd,
       decoder_7_segments_4_se, decoder_7_segments_4_sf, decoder_7_segments_4_sg, decoder_7_segments_4_sh,
       decoder_7_segments_5_sa, decoder_7_segments_5_sb, decoder_7_segments_5_sc, decoder_7_segments_5_sd,
       decoder_7_segments_5_se, decoder_7_segments_5_sf, decoder_7_segments_5_sg, decoder_7_segments_5_sh,
       no_delay_circulation_q, not_1_out, not_2_out, not_3_out, not_4_out, not_5_out, not_6_out, not_7_out,
       or_1_out;
  wire [3:0] counter_2_16_tunable_1_q, counter_2_16_tunable_2_q, counter_2_16_tunable_3_q,
       counter_2_16_tunable_4_q, counter_2_16_tunable_5_q, counter_2_16_tunable_6_q, full_adder_4_1_s,
       register_4_1_q, register_4_2_q, xnor_1_out;
  wire [7:0] register_8_1_q;

  Button button_1 (.out(button_1_out));
  Clock clock_1 (.out(clock_1_out));
  Button button_2 (.out(button_2_out));
  Clock clock_2 (.out(clock_2_out));
  Button button_3 (.out(button_3_out));
  Clock clock_3 (.out(clock_3_out));
  Button button_4 (.out(button_4_out));
  Clock clock_4 (.out(clock_4_out));
  Button button_5 (.out(button_5_out));
  Clock clk (.out(clk_out));
  Clock clock_5 (.out(clock_5_out));
  Button button_6 (.out(button_6_out));
  not not_1 (not_1_out, no_delay_circulation_q);
  not not_2 (not_2_out, d_flip_flop_r_1_q);
  not not_3 (not_3_out, d_flip_flop_r_negedge_1_q);
  not not_4 (not_4_out, d_flip_flop_r_en_1_q);
  not not_5 (not_5_out, clk_out);
  Clock clock_6 (.out(clock_6_out));
  Button button_7 (.out(button_7_out));
  Clock clock_7 (.out(clock_7_out));
  Button button_8 (.out(button_8_out));
  D_latch_R no_delay_circulation (.D(not_1_out), .WE(1'b1), .R(button_1_out), .Q(no_delay_circulation_q));  // open: Qn
  D_flip_flop_R d_flip_flop_r_1 (
    .D(not_2_out), .clk(clock_1_out), .R(button_2_out), .Q(d_flip_flop_r_1_q));  // open: Qn
  D_flip_flop_R_negedge d_flip_flop_r_negedge_1 (
    .D(not_3_out), .clk(clock_2_out), .R(button_3_out), .Q(d_flip_flop_r_negedge_1_q));  // open: Qn
  D_flip_flop_R_EN d_flip_flop_r_en_1 (
    .D(not_4_out), .clk(clock_3_out), .R(button_4_out), .EN(in_1), .Q(d_flip_flop_r_en_1_q));  // open: Qn
  register_4 register_4_1 (.D(in_2), .R(button_5_out), .clk(clock_4_out), .EN(in_3), .Q(register_4_1_q));
  or or_1 (or_1_out, R, d_flip_flop_r_en_7_q);
  and and_1 (and_1_out, counter_2_16_tunable_2_c, counter_2_16_tunable_1_c);
  and and_2 (and_2_out, counter_2_16_tunable_3_c, and_1_out);
  full_adder_4 full_adder_4_1 (.A(Q), .Ci(not_5_out), .B(4'b0000), .S(full_adder_4_1_s));  // open: Co
  counter_2_16_tunable counter_2_16_tunable_1 (
    .clk(clock_5_out), .R(button_6_out), .EN(in_9), .max(4'b1001), .Q(counter_2_16_tunable_1_q),
    .C(counter_2_16_tunable_1_c));
  D_flip_flop_R_EN d_flip_flop_r_en_2 (
    .D(counter_2_16_tunable_1_c), .clk(clock_5_out), .R(button_6_out), .EN(in_9), .Q(d_flip_flop_r_en_2_q));  // open: Qn
  counter_2_16_tunable counter_2_16_tunable_2 (
    .clk(d_flip_flop_r_en_2_q), .R(button_6_out), .EN(in_9), .max(4'b0101), .Q(counter_2_16_tunable_2_q),
    .C(counter_2_16_tunable_2_c));
  D_flip_flop_R_EN d_flip_flop_r_en_3 (
    .D(and_1_out), .clk(clock_5_out), .R(button_6_out), .EN(in_9), .Q(d_flip_flop_r_en_3_q));  // open: Qn
  counter_2_16_tunable counter_2_16_tunable_3 (
    .clk(d_flip_flop_r_en_3_q), .R(button_6_out), .EN(in_9), .max(4'b1001), .Q(counter_2_16_tunable_3_q),
    .C(counter_2_16_tunable_3_c));
  D_flip_flop_R_EN d_flip_flop_r_en_4 (
    .D(and_2_out), .clk(clock_5_out), .R(button_6_out), .EN(in_9), .Q(d_flip_flop_r_en_4_q));  // open: Qn
  counter_2_16_tunable counter_2_16_tunable_4 (
    .clk(d_flip_flop_r_en_4_q), .R(button_6_out), .EN(in_9), .max(4'b0101), .Q(counter_2_16_tunable_4_q));  // open: C
  counter_2_16_tunable counter_2_16_tunable_5 (
    .clk(clock_6_out), .R(button_7_out), .EN(not_6_out), .max(in_7), .Q(counter_2_16_tunable_5_q),
    .C(counter_2_16_tunable_5_c));
  register_4 register_4_2 (.D(out_12), .R(button_7_out), .clk(clock_6_out), .EN(not_6_out), .Q(register_4_2_q));
  D_flip_flop_R_EN d_flip_flop_r_en_5 (
    .D(counter_2_16_tunable_5_c), .clk(clock_6_out), .R(button_7_out), .EN(counter_2_16_tunable_5_c),
    .Q(d_flip_flop_r_en_5_q));  // open: Qn
  counter_2_16_tunable counter_2_16_tunable_6 (
    .clk(clock_7_out), .R(button_8_out), .EN(not_7_out), .max(in_8), .Q(counter_2_16_tunable_6_q),
    .C(counter_2_16_tunable_6_c));
  register_8 register_8_1 (.D(out_13), .R(button_8_out), .clk(clock_7_out), .EN(not_7_out), .Q(register_8_1_q));
  D_flip_flop_R_EN d_flip_flop_r_en_6 (
    .D(counter_2_16_tunable_6_c), .clk(clock_7_out), .R(button_8_out), .EN(counter_2_16_tunable_6_c),
    .Q(d_flip_flop_r_en_6_q));  // open: Qn
  not not_6 (not_6_out, d_flip_flop_r_en_5_q);
  not not_7 (not_7_out, d_flip_flop_r_en_6_q);
  decoder_7_segments decoder_7_segments_1 (
    .I3(register_4_1_q[3]), .I2(register_4_1_q[2]), .I1(register_4_1_q[1]), .I0(register_4_1_q[0]),
    .SA(decoder_7_segments_1_sa), .SB(decoder_7_segments_1_sb), .SC(decoder_7_segments_1_sc),
    .SD(decoder_7_segments_1_sd), .SE(decoder_7_segments_1_se), .SF(decoder_7_segments_1_sf),
    .SG(decoder_7_segments_1_sg), .SH(decoder_7_segments_1_sh));
  _7_Segment_Display u_7_segment_display_1 (
    .g(decoder_7_segments_1_sg), .f(decoder_7_segments_1_sf), .a(decoder_7_segments_1_sa),
    .b(decoder_7_segments_1_sb), .e(decoder_7_segments_1_se), .d(decoder_7_segments_1_sd),
    .c(decoder_7_segments_1_sc), .dp(decoder_7_segments_1_sh));
  register_4 register_4_3 (.D(full_adder_4_1_s), .R(or_1_out), .clk(clk_out), .EN(EN), .Q(Q));
  D_flip_flop_R_EN d_flip_flop_r_en_7 (
    .D(C), .clk(clk_out), .R(or_1_out), .EN(EN), .Q(d_flip_flop_r_en_7_q));  // open: Qn
  full_adder_4 full_adder_4_2 (.A(counter_2_16_tunable_5_q), .Ci(1'b0), .B(register_4_2_q), .S(out_12));  // open: Co
  full_adder_8_rev full_adder_8_rev_1 (
    .A(counter_2_16_tunable_6_q), .Ci(1'b0), .B(register_8_1_q), .S(out_13));  // open: Co
  decoder_7_segments decoder_7_segments_2 (
    .I3(counter_2_16_tunable_1_q[3]), .I2(counter_2_16_tunable_1_q[2]), .I1(counter_2_16_tunable_1_q[1]),
    .I0(counter_2_16_tunable_1_q[0]), .SA(decoder_7_segments_2_sa), .SB(decoder_7_segments_2_sb),
    .SC(decoder_7_segments_2_sc), .SD(decoder_7_segments_2_sd), .SE(decoder_7_segments_2_se),
    .SF(decoder_7_segments_2_sf), .SG(decoder_7_segments_2_sg), .SH(decoder_7_segments_2_sh));
  decoder_7_segments decoder_7_segments_3 (
    .I3(counter_2_16_tunable_2_q[3]), .I2(counter_2_16_tunable_2_q[2]), .I1(counter_2_16_tunable_2_q[1]),
    .I0(counter_2_16_tunable_2_q[0]), .SA(decoder_7_segments_3_sa), .SB(decoder_7_segments_3_sb),
    .SC(decoder_7_segments_3_sc), .SD(decoder_7_segments_3_sd), .SE(decoder_7_segments_3_se),
    .SF(decoder_7_segments_3_sf), .SG(decoder_7_segments_3_sg), .SH(decoder_7_segments_3_sh));
  decoder_7_segments decoder_7_segments_4 (
    .I3(counter_2_16_tunable_3_q[3]), .I2(counter_2_16_tunable_3_q[2]), .I1(counter_2_16_tunable_3_q[1]),
    .I0(counter_2_16_tunable_3_q[0]), .SA(decoder_7_segments_4_sa), .SB(decoder_7_segments_4_sb),
    .SC(decoder_7_segments_4_sc), .SD(decoder_7_segments_4_sd), .SE(decoder_7_segments_4_se),
    .SF(decoder_7_segments_4_sf), .SG(decoder_7_segments_4_sg), .SH(decoder_7_segments_4_sh));
  decoder_7_segments decoder_7_segments_5 (
    .I3(counter_2_16_tunable_4_q[3]), .I2(counter_2_16_tunable_4_q[2]), .I1(counter_2_16_tunable_4_q[1]),
    .I0(counter_2_16_tunable_4_q[0]), .SA(decoder_7_segments_5_sa), .SB(decoder_7_segments_5_sb),
    .SC(decoder_7_segments_5_sc), .SD(decoder_7_segments_5_sd), .SE(decoder_7_segments_5_se),
    .SF(decoder_7_segments_5_sf), .SG(decoder_7_segments_5_sg), .SH(decoder_7_segments_5_sh));
  assign xnor_1_out = ~(Q ^ max);  // XNOR_Gate xnor_1, 4 bits wide
  _7_Segment_Display u_7_segment_display_2 (
    .g(decoder_7_segments_2_sg), .f(decoder_7_segments_2_sf), .a(decoder_7_segments_2_sa),
    .b(decoder_7_segments_2_sb), .e(decoder_7_segments_2_se), .d(decoder_7_segments_2_sd),
    .c(decoder_7_segments_2_sc), .dp(decoder_7_segments_2_sh));
  _7_Segment_Display u_7_segment_display_3 (
    .g(decoder_7_segments_3_sg), .f(decoder_7_segments_3_sf), .a(decoder_7_segments_3_sa),
    .b(decoder_7_segments_3_sb), .e(decoder_7_segments_3_se), .d(decoder_7_segments_3_sd),
    .c(decoder_7_segments_3_sc), .dp(decoder_7_segments_3_sh));
  _7_Segment_Display u_7_segment_display_4 (
    .g(decoder_7_segments_4_sg), .f(decoder_7_segments_4_sf), .a(decoder_7_segments_4_sa),
    .b(decoder_7_segments_4_sb), .e(decoder_7_segments_4_se), .d(decoder_7_segments_4_sd),
    .c(decoder_7_segments_4_sc), .dp(decoder_7_segments_4_sh));
  _7_Segment_Display u_7_segment_display_5 (
    .g(decoder_7_segments_5_sg), .f(decoder_7_segments_5_sf), .a(decoder_7_segments_5_sa),
    .b(decoder_7_segments_5_sb), .e(decoder_7_segments_5_se), .d(decoder_7_segments_5_sd),
    .c(decoder_7_segments_5_sc), .dp(decoder_7_segments_5_sh));
  and and_3 (C, xnor_1_out[0], xnor_1_out[1], xnor_1_out[2], xnor_1_out[3]);
endmodule

module S_R_latch (
  input  S,
  input  R,
  output Q,
  output Qn
);

  wire dipswitch_1_p1, or_1_out, or_2_out;

  // DipSwitch #(.number(1)) dipswitch_1: pin names not known; wires that end beside it: dipswitch_1_p1
  or or_1 (or_1_out, S, dipswitch_1_p1);
  or or_2 (or_2_out, dipswitch_1_p1, R);
  nor nor_1 (Q, or_2_out, Qn);
  nor nor_2 (Qn, Q, or_1_out);
endmodule

module S_R_latch_NAND (
  input  Sn,
  input  Rn,
  output Q,
  output Qn
);

  wire dipswitch_1_p1, nor_1_out, nor_2_out;

  // DipSwitch #(.number(1)) dipswitch_1: pin names not known; wires that end beside it: dipswitch_1_p1
  nor nor_1 (nor_1_out, Sn, dipswitch_1_p1);
  nor nor_2 (nor_2_out, dipswitch_1_p1, Rn);
  nand nand_1 (Q, nor_2_out, Qn);
  nand nand_2 (Qn, Q, nor_1_out);
endmodule

module D_latch (
  input  D,
  input  WE,
  output Q,
  output Qn
);

  wire and_1_out, and_2_out, not_1_out;

  not not_1 (not_1_out, D);
  and and_1 (and_1_out, D, WE);
  and and_2 (and_2_out, WE, not_1_out);
  S_R_latch s_r_latch_1 (.S(and_1_out), .R(and_2_out), .Q(Q), .Qn(Qn));
endmodule

module D_latch_R (
  input  D,
  input  WE,
  input  R,
  output Q,
  output Qn
);

  wire and_1_out, and_2_out, and_3_out, not_1_out, not_2_out, or_1_out;

  not not_1 (not_1_out, R);
  and and_1 (and_1_out, D, not_1_out);
  or or_1 (or_1_out, WE, R);
  not not_2 (not_2_out, and_1_out);
  and and_2 (and_2_out, and_1_out, or_1_out);
  and and_3 (and_3_out, or_1_out, not_2_out);
  S_R_latch s_r_latch_1 (.S(and_2_out), .R(and_3_out), .Q(Q), .Qn(Qn));
endmodule

module D_flip_flop (
  input  D,
  input  clk,
  output Q,
  output Qn
);

  wire d_latch_1_q, not_1_out;

  not not_1 (not_1_out, clk);
  D_latch d_latch_1 (.D(D), .WE(not_1_out), .Q(d_latch_1_q));  // open: Qn
  D_latch d_latch_2 (.D(d_latch_1_q), .WE(clk), .Q(Q), .Qn(Qn));
endmodule

module D_flip_flop_R (
  input  D,
  input  clk,
  input  R,
  output Q,
  output Qn
);

  wire d_latch_r_1_q, not_1_out;

  not not_1 (not_1_out, clk);
  D_latch_R d_latch_r_1 (.D(D), .WE(not_1_out), .R(R), .Q(d_latch_r_1_q));  // open: Qn
  D_latch_R d_latch_r_2 (.D(d_latch_r_1_q), .WE(clk), .R(R), .Q(Q), .Qn(Qn));
endmodule

module D_flip_flop_R_negedge (
  input  D,
  input  clk,
  input  R,
  output Q,
  output Qn
);

  wire d_latch_r_1_q, not_1_out;

  not not_1 (not_1_out, clk);
  D_latch_R d_latch_r_1 (.D(D), .WE(clk), .R(R), .Q(d_latch_r_1_q));  // open: Qn
  D_latch_R d_latch_r_2 (.D(d_latch_r_1_q), .WE(not_1_out), .R(R), .Q(Q), .Qn(Qn));
endmodule

module D_flip_flop_R_EN (
  input  D,
  input  clk,
  input  R,
  input  EN,
  output Q,
  output Qn
);

  wire and_1_out, d_latch_r_1_q, not_1_out;

  not not_1 (not_1_out, clk);
  and and_1 (and_1_out, clk, EN);
  D_latch_R d_latch_r_1 (.D(D), .WE(not_1_out), .R(R), .Q(d_latch_r_1_q));  // open: Qn
  D_latch_R d_latch_r_2 (.D(d_latch_r_1_q), .WE(and_1_out), .R(R), .Q(Q), .Qn(Qn));
endmodule

module register_4 (
  input  [3:0] D,
  input  R,
  input  clk,
  input  EN,
  output [3:0] Q
);

  D_flip_flop_R_EN d_flip_flop_r_en_1 (.D(D[3]), .clk(clk), .R(R), .EN(EN), .Q(Q[3]));  // open: Qn
  D_flip_flop_R_EN d_flip_flop_r_en_2 (.D(D[2]), .clk(clk), .R(R), .EN(EN), .Q(Q[2]));  // open: Qn
  D_flip_flop_R_EN d_flip_flop_r_en_3 (.D(D[1]), .clk(clk), .R(R), .EN(EN), .Q(Q[1]));  // open: Qn
  D_flip_flop_R_EN d_flip_flop_r_en_4 (.D(D[0]), .clk(clk), .R(R), .EN(EN), .Q(Q[0]));  // open: Qn
endmodule

module decoder_7_segments (
  input  I3,
  input  I2,
  input  I1,
  input  I0,
  output SA,
  output SB,
  output SC,
  output SD,
  output SE,
  output SF,
  output SG,
  output SH
);

  wire M0_out, M1_out, M2_out, M3_out, M4_out, M5_out, M6_out, M7_out, M9_out, M10_out, M11_out, M12_out,
       M13_out, M14_out, M15_out, not_1_out, not_2_out, not_3_out, not_4_out;

  not not_1 (not_1_out, I3);
  not not_2 (not_2_out, I2);
  not not_3 (not_3_out, I1);
  not not_4 (not_4_out, I0);
  or M0 (M0_out, I3, I2, I1, I0);
  or M1 (M1_out, I3, I2, I1, not_4_out);
  or M2 (M2_out, I3, I2, not_3_out, I0);
  or M3 (M3_out, I3, I2, not_3_out, not_4_out);
  or M4 (M4_out, I3, not_2_out, I1, I0);
  or M5 (M5_out, I3, not_2_out, I1, not_4_out);
  or M6 (M6_out, I3, not_2_out, not_3_out, I0);
  or M7 (M7_out, I3, not_2_out, not_3_out, not_4_out);
  or M9 (M9_out, not_1_out, I2, I1, not_4_out);
  or M10 (M10_out, not_1_out, I2, not_3_out, I0);
  or M11 (M11_out, not_1_out, I2, not_3_out, not_4_out);
  or M12 (M12_out, not_1_out, not_2_out, I1, I0);
  or M13 (M13_out, not_1_out, not_2_out, I1, not_4_out);
  or M14 (M14_out, not_1_out, not_2_out, not_3_out, I0);
  or M15 (M15_out, not_1_out, not_2_out, not_3_out, not_4_out);
  and A (SA, M1_out, M4_out, M11_out, M13_out);
  and B (SB, M5_out, M6_out, M11_out, M12_out, M14_out, M15_out);
  and C (SC, M2_out, M12_out, M14_out, M15_out);
  and D (SD, M1_out, M4_out, M7_out, M10_out, M15_out);
  and E (SE, M1_out, M3_out, M4_out, M5_out, M7_out, M9_out);
  and F (SF, M1_out, M2_out, M3_out, M7_out, M13_out);
  and G (SG, M0_out, M1_out, M7_out, M12_out);

  assign SH = 1'b0;
endmodule

module full_adder_1 (
  input  A,
  input  B,
  input  Ci,
  output S,
  output Co
);

  wire and_1_out, and_2_out, and_3_out, xor_1_out;

  xor xor_1 (xor_1_out, A, B);
  and and_1 (and_1_out, A, B);
  and and_2 (and_2_out, A, Ci);
  and and_3 (and_3_out, B, Ci);
  xor xor_2 (S, xor_1_out, Ci);
  or or_1 (Co, and_1_out, and_2_out, and_3_out);
endmodule

module full_adder_4 (
  input  [3:0] A,
  input  Ci,
  input  [3:0] B,
  output [3:0] S,
  output Co
);

  wire full_adder_1_1_co, full_adder_1_2_co, full_adder_1_3_co;

  full_adder_1 full_adder_1_1 (.A(A[0]), .B(B[0]), .Ci(Ci), .S(S[0]), .Co(full_adder_1_1_co));
  full_adder_1 full_adder_1_2 (.A(A[1]), .B(B[1]), .Ci(full_adder_1_1_co), .S(S[1]), .Co(full_adder_1_2_co));
  full_adder_1 full_adder_1_3 (.A(A[2]), .B(B[2]), .Ci(full_adder_1_2_co), .S(S[2]), .Co(full_adder_1_3_co));
  full_adder_1 full_adder_1_4 (.A(A[3]), .B(B[3]), .Ci(full_adder_1_3_co), .S(S[3]), .Co(Co));
endmodule

module counter_2_16_tunable (
  input  clk,
  input  R,
  input  EN,
  input  [3:0] max,
  output [3:0] Q,
  output C
);

  wire d_flip_flop_r_en_1_q, not_1_out, or_1_out;
  wire [3:0] full_adder_4_1_s, xnor_1_out;

  not not_1 (not_1_out, clk);
  or or_1 (or_1_out, R, d_flip_flop_r_en_1_q);
  full_adder_4 full_adder_4_1 (.A(Q), .Ci(not_1_out), .B(4'b0000), .S(full_adder_4_1_s));  // open: Co
  D_flip_flop_R_EN d_flip_flop_r_en_1 (.D(C), .clk(clk), .R(or_1_out), .EN(EN), .Q(d_flip_flop_r_en_1_q));  // open: Qn
  register_4 register_4_1 (.D(full_adder_4_1_s), .R(or_1_out), .clk(clk), .EN(EN), .Q(Q));
  assign xnor_1_out = ~(Q ^ max);  // XNOR_Gate xnor_1, 4 bits wide
  and and_1 (C, xnor_1_out[0], xnor_1_out[1], xnor_1_out[2], xnor_1_out[3]);
endmodule

module register_8 (
  input  [7:0] D,
  input  R,
  input  clk,
  input  EN,
  output [7:0] Q
);

  D_flip_flop_R_EN d_flip_flop_r_en_1 (.D(D[7]), .clk(clk), .R(R), .EN(EN), .Q(Q[7]));  // open: Qn
  D_flip_flop_R_EN d_flip_flop_r_en_2 (.D(D[6]), .clk(clk), .R(R), .EN(EN), .Q(Q[6]));  // open: Qn
  D_flip_flop_R_EN d_flip_flop_r_en_3 (.D(D[5]), .clk(clk), .R(R), .EN(EN), .Q(Q[5]));  // open: Qn
  D_flip_flop_R_EN d_flip_flop_r_en_4 (.D(D[4]), .clk(clk), .R(R), .EN(EN), .Q(Q[4]));  // open: Qn
  D_flip_flop_R_EN d_flip_flop_r_en_5 (.D(D[3]), .clk(clk), .R(R), .EN(EN), .Q(Q[3]));  // open: Qn
  D_flip_flop_R_EN d_flip_flop_r_en_6 (.D(D[2]), .clk(clk), .R(R), .EN(EN), .Q(Q[2]));  // open: Qn
  D_flip_flop_R_EN d_flip_flop_r_en_7 (.D(D[1]), .clk(clk), .R(R), .EN(EN), .Q(Q[1]));  // open: Qn
  D_flip_flop_R_EN d_flip_flop_r_en_8 (.D(D[0]), .clk(clk), .R(R), .EN(EN), .Q(Q[0]));  // open: Qn
endmodule

module full_adder_8_rev (
  input  [3:0] A,
  input  Ci,
  input  [7:0] B,
  output [7:0] S,
  output Co
);

  wire full_adder_1_1_co, full_adder_1_2_co, full_adder_1_3_co, full_adder_1_4_co, full_adder_1_5_co,
       full_adder_1_6_co, full_adder_1_7_co;

  full_adder_1 full_adder_1_1 (.A(A[0]), .B(B[0]), .Ci(Ci), .S(S[0]), .Co(full_adder_1_1_co));
  full_adder_1 full_adder_1_2 (.A(A[1]), .B(B[1]), .Ci(full_adder_1_1_co), .S(S[1]), .Co(full_adder_1_2_co));
  full_adder_1 full_adder_1_3 (.A(A[2]), .B(B[2]), .Ci(full_adder_1_2_co), .S(S[2]), .Co(full_adder_1_3_co));
  full_adder_1 full_adder_1_4 (.A(A[3]), .B(B[3]), .Ci(full_adder_1_3_co), .S(S[3]), .Co(full_adder_1_4_co));
  full_adder_1 full_adder_1_5 (.A(1'b0), .B(B[4]), .Ci(full_adder_1_4_co), .S(S[4]), .Co(full_adder_1_5_co));
  full_adder_1 full_adder_1_6 (.A(1'b0), .B(B[5]), .Ci(full_adder_1_5_co), .S(S[5]), .Co(full_adder_1_6_co));
  full_adder_1 full_adder_1_7 (.A(1'b0), .B(B[6]), .Ci(full_adder_1_6_co), .S(S[6]), .Co(full_adder_1_7_co));
  full_adder_1 full_adder_1_8 (.A(1'b0), .B(B[7]), .Ci(full_adder_1_7_co), .S(S[7]), .Co(Co));
endmodule

module register_2 (
  input  [1:0] D,
  input  R,
  input  clk,
  input  EN,
  output [1:0] Q
);

  D_flip_flop_R_EN d_flip_flop_r_en_1 (.D(D[1]), .clk(clk), .R(R), .EN(EN), .Q(Q[1]));  // open: Qn
  D_flip_flop_R_EN d_flip_flop_r_en_2 (.D(D[0]), .clk(clk), .R(R), .EN(EN), .Q(Q[0]));  // open: Qn
endmodule

module counter_2_16_tunable_rev (
  input  [3:0] D,
  input  LD,
  input  clk,
  input  R,
  input  EN,
  input  [3:0] max,
  output [3:0] Q,
  output C
);

  wire d_flip_flop_r_en_1_q, not_1_out, or_1_out;
  wire [3:0] full_adder_4_1_s, selector_2_1_4bits_1_y, xnor_1_out;

  not not_1 (not_1_out, clk);
  or or_1 (or_1_out, R, d_flip_flop_r_en_1_q);
  full_adder_4 full_adder_4_1 (.A(Q), .Ci(not_1_out), .B(4'b0000), .S(full_adder_4_1_s));  // open: Co
  D_flip_flop_R_EN d_flip_flop_r_en_1 (.D(C), .clk(clk), .R(or_1_out), .EN(EN), .Q(d_flip_flop_r_en_1_q));  // open: Qn
  selector_2_1_4bits selector_2_1_4bits_1 (.D1(D), .D0(full_adder_4_1_s), .S(LD), .Y(selector_2_1_4bits_1_y));
  assign xnor_1_out = ~(Q ^ max);  // XNOR_Gate xnor_1, 4 bits wide
  and and_1 (C, xnor_1_out[0], xnor_1_out[1], xnor_1_out[2], xnor_1_out[3]);
  register_4 register_4_1 (.D(selector_2_1_4bits_1_y), .R(or_1_out), .clk(clk), .EN(EN), .Q(Q));
endmodule

module selector_2_1 (
  input  D1,
  input  D0,
  input  S,
  output Y
);

  wire and_1_out, and_2_out, not_1_out;

  not not_1 (not_1_out, S);
  and and_1 (and_1_out, D1, S);
  and and_2 (and_2_out, D0, not_1_out);
  or or_1 (Y, and_1_out, and_2_out);
endmodule

module selector_2_1_4bits (
  input  [3:0] D1,
  input  [3:0] D0,
  input  S,
  output [3:0] Y
);

  selector_2_1 selector_2_1_1 (.D1(D1[3]), .D0(D0[3]), .S(S), .Y(Y[3]));
  selector_2_1 selector_2_1_2 (.D1(D1[2]), .D0(D0[2]), .S(S), .Y(Y[2]));
  selector_2_1 selector_2_1_3 (.D1(D1[1]), .D0(D0[1]), .S(S), .Y(Y[1]));
  selector_2_1 selector_2_1_4 (.D1(D1[0]), .D0(D0[0]), .S(S), .Y(Y[0]));
endmodule
