// Logisim project F5.circ as structural Verilog: 13 circuits, main circuit workplace_F5
module workplace_F5 (
  input  [7:0] cmd_15,
  input  [7:0] cmd_14,
  input  [7:0] cmd_13,
  input  [7:0] cmd_12,
  input  [7:0] cmd_11,
  input  [7:0] cmd_10,
  input  [7:0] cmd_9,
  input  [7:0] cmd_8,
  input  R,
  input  [7:0] cmd_7,
  input  [7:0] cmd_6,
  input  EN,
  input  [7:0] cmd_5,
  input  [7:0] cmd_4,
  input  [7:0] cmd_3,
  input  [7:0] cmd_2,
  input  [7:0] cmd_1,
  input  [7:0] cmd_0,
  input  [3:0] cmd_max,
  output [7:0] current_cmd,
  output [7:0] output_display
);

  wire and_1_out, and_2_out, clk_out, cmd_bner0_y, cmd_decoder_y0, cmd_decoder_y2, cmd_decoder_y3,
       d_flip_flop_r_1_q, decoder_7_segments_1_sa, decoder_7_segments_1_sb, decoder_7_segments_1_sc,
       decoder_7_segments_1_sd, decoder_7_segments_1_se, decoder_7_segments_1_sf, decoder_7_segments_1_sg,
       decoder_7_segments_1_sh, decoder_7_segments_2_sa, decoder_7_segments_2_sb, decoder_7_segments_2_sc,
       decoder_7_segments_2_sd, decoder_7_segments_2_se, decoder_7_segments_2_sf, decoder_7_segments_2_sg,
       decoder_7_segments_2_sh, not_1_out, not_2_out, not_3_out, or_1_out, write_EN_pre_q;
  wire [1:0] selector_4_1_2bits_1_data, write_addr_pre_q;
  wire [3:0] PC_q;
  wire [7:0] cmd_add_s, GPR_read_data_1, GPR_read_data_2, register_8_1_q, register_8_2_q,
       selector_4_1_8bits_1_y;

  Clock clk (.out(clk_out));
  and and_1 (and_1_out, ~cmd_bner0_y, cmd_decoder_y3);  // AND_Gate
  counter_2_16_tunable_rev PC (
    .D(current_cmd[5:2]), .LD(and_1_out), .clk(clk_out), .R(R), .EN(EN), .max(cmd_max), .Q(PC_q));  // open: C
  or or_1 (or_1_out, cmd_decoder_y2, cmd_decoder_y0);
  D_flip_flop_R_EN write_EN_pre (.D(or_1_out), .clk(clk_out), .R(R), .EN(EN), .Q(write_EN_pre_q));  // open: Qn
  not not_1 (not_1_out, clk_out);
  not not_2 (not_2_out, current_cmd[7]);
  ROM_16_1_8bits cmd (
    .D15(cmd_15), .D14(cmd_14), .D13(cmd_13), .D12(cmd_12), .D11(cmd_11), .D10(cmd_10), .D9(cmd_9),
    .D8(cmd_8), .addr(PC_q), .D7(cmd_7), .D6(cmd_6), .D5(cmd_5), .D4(cmd_4), .D3(cmd_3), .D2(cmd_2),
    .D1(cmd_1), .D0(cmd_0), .data(current_cmd));
  register_8 register_8_1 (.D(selector_4_1_8bits_1_y), .R(R), .clk(clk_out), .EN(write_EN_pre_q), .Q(register_8_1_q));
  RAM_4_1_8bits_rev GPR (
    .write_data(register_8_1_q), .R(R), .clk(not_1_out), .write_EN(write_EN_pre_q),
    .write_addr(write_addr_pre_q), .read_addr_1(selector_4_1_2bits_1_data), .read_addr_2(current_cmd[1:0]),
    .read_data_1(GPR_read_data_1), .read_data_2(GPR_read_data_2));
  register_2 write_addr_pre (.D(current_cmd[5:4]), .R(R), .clk(clk_out), .EN(write_EN_pre_q), .Q(write_addr_pre_q));
  selector_4_1_2bits selector_4_1_2bits_1 (
    .D3(2'b00), .D0(current_cmd[3:2]), .addr(current_cmd[7:6]), .data(selector_4_1_2bits_1_data));  // open: D2, D1
  and and_2 (and_2_out, current_cmd[6], not_2_out);
  full_adder_8 cmd_add (.A(GPR_read_data_1), .B(GPR_read_data_2), .S(cmd_add_s));  // open: Ci, Co
  D_flip_flop_R d_flip_flop_r_1 (.D(and_2_out), .clk(clk_out), .R(R), .Q(d_flip_flop_r_1_q));  // open: Qn
  decoder_2_4 cmd_decoder (
    .A1(current_cmd[7]), .A0(current_cmd[6]), .Y3(cmd_decoder_y3), .Y2(cmd_decoder_y2), .Y0(cmd_decoder_y0));  // open: Y1
  selector_4_1_8bits selector_4_1_8bits_1 (
    .D2({4'b0000, current_cmd[3:0]}), .D0(cmd_add_s), .addr(current_cmd[7:6]), .Y(selector_4_1_8bits_1_y));  // open: D3, D1
  not not_3 (not_3_out, clk_out);
  comparator_8 cmd_bner0 (.A(GPR_read_data_1), .B(GPR_read_data_2), .Y(cmd_bner0_y));
  register_8 register_8_2 (.D(GPR_read_data_2), .R(R), .clk(clk_out), .EN(d_flip_flop_r_1_q), .Q(register_8_2_q));
  register_8 cmd_out (.D(register_8_2_q), .R(R), .clk(not_3_out), .EN(d_flip_flop_r_1_q), .Q(output_display));
  decoder_7_segments decoder_7_segments_1 (
    .I3(output_display[3]), .I2(output_display[2]), .I1(output_display[1]), .I0(output_display[0]),
    .SA(decoder_7_segments_1_sa), .SB(decoder_7_segments_1_sb), .SC(decoder_7_segments_1_sc),
    .SD(decoder_7_segments_1_sd), .SE(decoder_7_segments_1_se), .SF(decoder_7_segments_1_sf),
    .SG(decoder_7_segments_1_sg), .SH(decoder_7_segments_1_sh));
  decoder_7_segments decoder_7_segments_2 (
    .I3(output_display[7]), .I2(output_display[6]), .I1(output_display[5]), .I0(output_display[4]),
    .SA(decoder_7_segments_2_sa), .SB(decoder_7_segments_2_sb), .SC(decoder_7_segments_2_sc),
    .SD(decoder_7_segments_2_sd), .SE(decoder_7_segments_2_se), .SF(decoder_7_segments_2_sf),
    .SG(decoder_7_segments_2_sg), .SH(decoder_7_segments_2_sh));
  _7_Segment_Display u_7_segment_display_1 (
    .g(decoder_7_segments_2_sg), .f(decoder_7_segments_2_sf), .a(decoder_7_segments_2_sa),
    .b(decoder_7_segments_2_sb), .e(decoder_7_segments_2_se), .d(decoder_7_segments_2_sd),
    .c(decoder_7_segments_2_sc), .dp(decoder_7_segments_2_sh));
  _7_Segment_Display u_7_segment_display_2 (
    .g(decoder_7_segments_1_sg), .f(decoder_7_segments_1_sf), .a(decoder_7_segments_1_sa),
    .b(decoder_7_segments_1_sb), .e(decoder_7_segments_1_se), .d(decoder_7_segments_1_sd),
    .c(decoder_7_segments_1_sc), .dp(decoder_7_segments_1_sh));
endmodule

module selector_8_1 (
  input  D7,
  input  D6,
  input  D5,
  input  D4,
  input  D3,
  input  D2,
  input  D1,
  input  D0,
  input  S2,
  input  S1,
  input  S0,
  output Y
);

  wire and_1_out, and_2_out, and_3_out, and_4_out, and_5_out, and_6_out, and_7_out, and_8_out, not_1_out,
       not_2_out, not_3_out, or_1_out, or_2_out;

  not not_1 (not_1_out, S2);
  not not_2 (not_2_out, S1);
  not not_3 (not_3_out, S0);
  and and_1 (and_1_out, not_1_out, not_2_out, not_3_out, D0);
  and and_2 (and_2_out, not_1_out, not_2_out, S0, D1);
  and and_3 (and_3_out, not_1_out, S1, not_3_out, D2);
  and and_4 (and_4_out, not_1_out, S1, S0, D3);
  and and_5 (and_5_out, S2, not_2_out, not_3_out, D4);
  and and_6 (and_6_out, S2, not_2_out, S0, D5);
  and and_7 (and_7_out, S2, S1, not_3_out, D6);
  and and_8 (and_8_out, S2, S1, S0, D7);
  or or_1 (or_1_out, and_1_out, and_2_out, and_3_out, and_4_out);
  or or_2 (or_2_out, and_5_out, and_6_out, and_7_out, and_8_out);
  or or_3 (Y, or_1_out, or_2_out);
endmodule

module ROM_8_1_8bits (
  input  [7:0] D7,
  input  [7:0] D6,
  input  [7:0] D5,
  input  [7:0] D4,
  input  [7:0] D3,
  input  [7:0] D2,
  input  [7:0] D1,
  input  [7:0] D0,
  input  [2:0] addr,
  output [7:0] data
);

  selector_8_1 selector_8_1_1 (
    .D7(D7[7]), .D6(D6[7]), .D5(D5[7]), .D4(D4[7]), .D3(D3[7]), .D2(D2[7]), .D1(D1[7]), .D0(D0[7]),
    .S2(addr[2]), .S1(addr[1]), .S0(addr[0]), .Y(data[7]));
  selector_8_1 selector_8_1_2 (
    .D7(D7[6]), .D6(D6[6]), .D5(D5[6]), .D4(D4[6]), .D3(D3[6]), .D2(D2[6]), .D1(D1[6]), .D0(D0[6]),
    .S2(addr[2]), .S1(addr[1]), .S0(addr[0]), .Y(data[6]));
  selector_8_1 selector_8_1_3 (
    .D7(D7[5]), .D6(D6[5]), .D5(D5[5]), .D4(D4[5]), .D3(D3[5]), .D2(D2[5]), .D1(D1[5]), .D0(D0[5]),
    .S2(addr[2]), .S1(addr[1]), .S0(addr[0]), .Y(data[5]));
  selector_8_1 selector_8_1_4 (
    .D7(D7[4]), .D6(D6[4]), .D5(D5[4]), .D4(D4[4]), .D3(D3[4]), .D2(D2[4]), .D1(D1[4]), .D0(D0[4]),
    .S2(addr[2]), .S1(addr[1]), .S0(addr[0]), .Y(data[4]));
  selector_8_1 selector_8_1_5 (
    .D7(D7[3]), .D6(D6[3]), .D5(D5[3]), .D4(D4[3]), .D3(D3[3]), .D2(D2[3]), .D1(D1[3]), .D0(D0[3]),
    .S2(addr[2]), .S1(addr[1]), .S0(addr[0]), .Y(data[3]));
  selector_8_1 selector_8_1_6 (
    .D7(D7[2]), .D6(D6[2]), .D5(D5[2]), .D4(D4[2]), .D3(D3[2]), .D2(D2[2]), .D1(D1[2]), .D0(D0[2]),
    .S2(addr[2]), .S1(addr[1]), .S0(addr[0]), .Y(data[2]));
  selector_8_1 selector_8_1_7 (
    .D7(D7[1]), .D6(D6[1]), .D5(D5[1]), .D4(D4[1]), .D3(D3[1]), .D2(D2[1]), .D1(D1[1]), .D0(D0[1]),
    .S2(addr[2]), .S1(addr[1]), .S0(addr[0]), .Y(data[1]));
  selector_8_1 selector_8_1_8 (
    .D7(D7[0]), .D6(D6[0]), .D5(D5[0]), .D4(D4[0]), .D3(D3[0]), .D2(D2[0]), .D1(D1[0]), .D0(D0[0]),
    .S2(addr[2]), .S1(addr[1]), .S0(addr[0]), .Y(data[0]));
endmodule

module ROM_16_1_8bits (
  input  [7:0] D15,
  input  [7:0] D14,
  input  [7:0] D13,
  input  [7:0] D12,
  input  [7:0] D11,
  input  [7:0] D10,
  input  [7:0] D9,
  input  [7:0] D8,
  input  [3:0] addr,
  input  [7:0] D7,
  input  [7:0] D6,
  input  [7:0] D5,
  input  [7:0] D4,
  input  [7:0] D3,
  input  [7:0] D2,
  input  [7:0] D1,
  input  [7:0] D0,
  output [7:0] data
);

  wire [7:0] rom_8_1_8bits_1_data, rom_8_1_8bits_2_data;

  ROM_8_1_8bits rom_8_1_8bits_1 (
    .D7(D15), .D6(D14), .D5(D13), .D4(D12), .D3(D11), .D2(D10), .D1(D9), .D0(D8), .addr(addr[2:0]),
    .data(rom_8_1_8bits_1_data));
  ROM_8_1_8bits rom_8_1_8bits_2 (
    .D7(D7), .D6(D6), .D5(D5), .D4(D4), .D3(D3), .D2(D2), .D1(D1), .D0(D0), .addr(addr[2:0]),
    .data(rom_8_1_8bits_2_data));
  selector_2_1 selector_2_1_1 (.D0(rom_8_1_8bits_2_data[7]), .S(addr[3]), .D1(rom_8_1_8bits_1_data[7]), .Y(data[7]));
  selector_2_1 selector_2_1_2 (.D0(rom_8_1_8bits_2_data[6]), .S(addr[3]), .D1(rom_8_1_8bits_1_data[6]), .Y(data[6]));
  selector_2_1 selector_2_1_3 (.D0(rom_8_1_8bits_2_data[5]), .S(addr[3]), .D1(rom_8_1_8bits_1_data[5]), .Y(data[5]));
  selector_2_1 selector_2_1_4 (.D0(rom_8_1_8bits_2_data[4]), .S(addr[3]), .D1(rom_8_1_8bits_1_data[4]), .Y(data[4]));
  selector_2_1 selector_2_1_5 (.D0(rom_8_1_8bits_2_data[3]), .S(addr[3]), .D1(rom_8_1_8bits_1_data[3]), .Y(data[3]));
  selector_2_1 selector_2_1_6 (.D0(rom_8_1_8bits_2_data[2]), .S(addr[3]), .D1(rom_8_1_8bits_1_data[2]), .Y(data[2]));
  selector_2_1 selector_2_1_7 (.D0(rom_8_1_8bits_2_data[1]), .S(addr[3]), .D1(rom_8_1_8bits_1_data[1]), .Y(data[1]));
  selector_2_1 selector_2_1_8 (.D0(rom_8_1_8bits_2_data[0]), .S(addr[3]), .D1(rom_8_1_8bits_1_data[0]), .Y(data[0]));
endmodule

module selector_2_1 (
  input  D0,
  input  S,
  input  D1,
  output Y
);

  wire and_1_out, and_2_out, not_1_out;

  not not_1 (not_1_out, S);
  and and_1 (and_1_out, D0, not_1_out);
  and and_2 (and_2_out, S, D1);
  or or_1 (Y, and_1_out, and_2_out);
endmodule

module selector_4_1 (
  input  D3,
  input  D2,
  input  D1,
  input  D0,
  input  S1,
  input  S0,
  output Y
);

  wire and_1_out, and_2_out, and_3_out, and_4_out, not_1_out, not_2_out;

  not not_1 (not_1_out, S1);
  not not_2 (not_2_out, S0);
  and and_1 (and_1_out, not_1_out, not_2_out, D0);
  and and_2 (and_2_out, not_1_out, S0, D1);
  and and_3 (and_3_out, S1, not_2_out, D2);
  and and_4 (and_4_out, S1, S0, D3);
  or or_1 (Y, and_1_out, and_2_out, and_3_out, and_4_out);
endmodule

module selector_4_1_8bits (
  input  [7:0] D3,
  input  [7:0] D2,
  input  [7:0] D1,
  input  [7:0] D0,
  input  [1:0] addr,
  output [7:0] Y
);

  selector_4_1 selector_4_1_1 (.D3(D3[7]), .D2(D2[7]), .D1(D1[7]), .D0(D0[7]), .S1(addr[1]), .S0(addr[0]), .Y(Y[7]));
  selector_4_1 selector_4_1_2 (.D3(D3[6]), .D2(D2[6]), .D1(D1[6]), .D0(D0[6]), .S1(addr[1]), .S0(addr[0]), .Y(Y[6]));
  selector_4_1 selector_4_1_3 (.D3(D3[5]), .D2(D2[5]), .D1(D1[5]), .D0(D0[5]), .S1(addr[1]), .S0(addr[0]), .Y(Y[5]));
  selector_4_1 selector_4_1_4 (.D3(D3[4]), .D2(D2[4]), .D1(D1[4]), .D0(D0[4]), .S1(addr[1]), .S0(addr[0]), .Y(Y[4]));
  selector_4_1 selector_4_1_5 (.D3(D3[3]), .D2(D2[3]), .D1(D1[3]), .D0(D0[3]), .S1(addr[1]), .S0(addr[0]), .Y(Y[3]));
  selector_4_1 selector_4_1_6 (.D3(D3[2]), .D2(D2[2]), .D1(D1[2]), .D0(D0[2]), .S1(addr[1]), .S0(addr[0]), .Y(Y[2]));
  selector_4_1 selector_4_1_7 (.D3(D3[1]), .D2(D2[1]), .D1(D1[1]), .D0(D0[1]), .S1(addr[1]), .S0(addr[0]), .Y(Y[1]));
  selector_4_1 selector_4_1_8 (.D3(D3[0]), .D2(D2[0]), .D1(D1[0]), .D0(D0[0]), .S1(addr[1]), .S0(addr[0]), .Y(Y[0]));
endmodule

module RAM_4_1_8bits (
  input  [7:0] write_data,
  input  R,
  input  clk,
  input  EN,
  input  [1:0] addr,
  output [7:0] output_data
);

  wire and_1_out, and_2_out, and_3_out, and_4_out, not_1_out, not_2_out;
  wire [7:0] register_8_1_q, register_8_2_q, register_8_3_q, register_8_4_q;

  and and_1 (and_1_out, addr[1], addr[0], EN);
  and and_2 (and_2_out, not_1_out, addr[1], EN);
  and and_3 (and_3_out, addr[0], not_2_out, EN);
  and and_4 (and_4_out, not_2_out, not_1_out, EN);
  not not_1 (not_1_out, addr[0]);
  not not_2 (not_2_out, addr[1]);
  register_8 register_8_1 (.D(write_data), .R(R), .clk(clk), .EN(and_1_out), .Q(register_8_1_q));
  register_8 register_8_2 (.D(write_data), .R(R), .clk(clk), .EN(and_2_out), .Q(register_8_2_q));
  register_8 register_8_3 (.D(write_data), .R(R), .clk(clk), .EN(and_3_out), .Q(register_8_3_q));
  register_8 register_8_4 (.D(write_data), .R(R), .clk(clk), .EN(and_4_out), .Q(register_8_4_q));
  selector_4_1_8bits selector_4_1_8bits_1 (
    .D3(register_8_1_q), .D2(register_8_2_q), .D1(register_8_3_q), .D0(register_8_4_q), .addr(addr),
    .Y(output_data));
endmodule

module decoder_2_4 (
  input  A1,
  input  A0,
  output Y3,
  output Y2,
  output Y1,
  output Y0
);

  wire not_1_out, not_2_out;

  not not_1 (not_1_out, A1);
  not not_2 (not_2_out, A0);
  and and_1 (Y3, A1, A0);
  and and_2 (Y2, A1, not_2_out);
  and and_3 (Y1, not_1_out, A0);
  and and_4 (Y0, not_1_out, not_2_out);
endmodule

module RAM_4_1_8bits_rev (
  input  [7:0] write_data,
  input  R,
  input  clk,
  input  write_EN,
  input  [1:0] write_addr,
  input  [1:0] read_addr_1,
  input  [1:0] read_addr_2,
  output [7:0] read_data_1,
  output [7:0] read_data_2
);

  wire and_1_out, and_2_out, and_3_out, and_4_out, not_1_out, not_2_out;
  wire [7:0] register_8_1_q, register_8_2_q, register_8_3_q, register_8_4_q;

  and and_1 (and_1_out, write_addr[1], write_addr[0], write_EN);
  and and_2 (and_2_out, not_1_out, write_addr[1], write_EN);
  and and_3 (and_3_out, write_addr[0], not_2_out, write_EN);
  and and_4 (and_4_out, not_2_out, not_1_out, write_EN);
  not not_1 (not_1_out, write_addr[0]);
  not not_2 (not_2_out, write_addr[1]);
  register_8 register_8_1 (.D(write_data), .R(R), .clk(clk), .EN(and_1_out), .Q(register_8_1_q));
  register_8 register_8_2 (.D(write_data), .R(R), .clk(clk), .EN(and_2_out), .Q(register_8_2_q));
  register_8 register_8_3 (.D(write_data), .R(R), .clk(clk), .EN(and_3_out), .Q(register_8_3_q));
  register_8 register_8_4 (.D(write_data), .R(R), .clk(clk), .EN(and_4_out), .Q(register_8_4_q));
  selector_4_1_8bits selector_4_1_8bits_1 (
    .D3(register_8_1_q), .D2(register_8_2_q), .D1(register_8_3_q), .D0(register_8_4_q), .addr(read_addr_1),
    .Y(read_data_1));
  selector_4_1_8bits selector_4_1_8bits_2 (
    .D3(register_8_1_q), .D2(register_8_2_q), .D1(register_8_3_q), .D0(register_8_4_q), .addr(read_addr_2),
    .Y(read_data_2));
endmodule

module full_adder_8 (
  input  [7:0] A,
  input  Ci,
  input  [7:0] B,
  output [7:0] S,
  output Co
);

  wire full_adder_1_1_co, full_adder_1_2_co, full_adder_1_3_co, full_adder_1_4_co, full_adder_1_5_co,
       full_adder_1_6_co, full_adder_1_7_co;

  full_adder_1 full_adder_1_1 (.A(A[0]), .B(B[0]), .Ci(Ci), .S(S[0]), .Co(full_adder_1_1_co));
  full_adder_1 full_adder_1_2 (.A(A[1]), .B(B[1]), .Ci(full_adder_1_1_co), .S(S[1]), .Co(full_adder_1_2_co));
  full_adder_1 full_adder_1_3 (.A(A[2]), .B(B[2]), .Ci(full_adder_1_2_co), .S(S[2]), .Co(full_adder_1_3_co));
  full_adder_1 full_adder_1_4 (.A(A[3]), .B(B[3]), .Ci(full_adder_1_3_co), .S(S[3]), .Co(full_adder_1_4_co));
  full_adder_1 full_adder_1_5 (.A(A[4]), .B(B[4]), .Ci(full_adder_1_4_co), .S(S[4]), .Co(full_adder_1_5_co));
  full_adder_1 full_adder_1_6 (.A(A[5]), .B(B[5]), .Ci(full_adder_1_5_co), .S(S[5]), .Co(full_adder_1_6_co));
  full_adder_1 full_adder_1_7 (.A(A[6]), .B(B[6]), .Ci(full_adder_1_6_co), .S(S[6]), .Co(full_adder_1_7_co));
  full_adder_1 full_adder_1_8 (.A(A[7]), .B(B[7]), .Ci(full_adder_1_7_co), .S(S[7]), .Co(Co));
endmodule

module selector_4_1_2bits (
  input  [1:0] D3,
  input  [1:0] D2,
  input  [1:0] D1,
  input  [1:0] D0,
  input  [1:0] addr,
  output [1:0] data
);

  selector_4_1 selector_4_1_1 (.D3(D3[1]), .D2(D2[1]), .D1(D1[1]), .D0(D0[1]), .S1(addr[1]), .S0(addr[0]), .Y(data[1]));
  selector_4_1 selector_4_1_2 (.D3(D3[0]), .D2(D2[0]), .D1(D1[0]), .D0(D0[0]), .S1(addr[1]), .S0(addr[0]), .Y(data[0]));
endmodule

module comparator_8 (
  input  [7:0] A,
  input  [7:0] B,
  output Y
);

  wire xnor_1_out, xnor_2_out, xnor_3_out, xnor_4_out, xnor_5_out, xnor_6_out, xnor_7_out, xnor_8_out;

  xnor xnor_1 (xnor_1_out, A[0], B[0]);
  xnor xnor_2 (xnor_2_out, A[1], B[1]);
  xnor xnor_3 (xnor_3_out, A[2], B[2]);
  xnor xnor_4 (xnor_4_out, A[3], B[3]);
  xnor xnor_5 (xnor_5_out, A[4], B[4]);
  xnor xnor_6 (xnor_6_out, A[5], B[5]);
  xnor xnor_7 (xnor_7_out, A[6], B[6]);
  xnor xnor_8 (xnor_8_out, A[7], B[7]);
  and and_1 (Y, xnor_1_out, xnor_2_out, xnor_3_out, xnor_4_out, xnor_5_out, xnor_6_out, xnor_7_out, xnor_8_out);
endmodule
