// Logisim project test.circ as structural Verilog: 1 circuit, main circuit main
module main (
  input  x,
  input  y,
  output z
);

  wire and_1_out, and_2_out, not_1_out, not_2_out;

  not not_1 (not_1_out, y);
  not not_2 (not_2_out, x);
  and and_1 (and_1_out, x, not_1_out);
  and and_2 (and_2_out, not_2_out, y);
  or or_1 (z, and_1_out, and_2_out);

  // Notes on the sheet:
  //   XOR
  //   AND 1
  //   AND 2
  //   OR
endmodule
