// Logisim project F3.4.circ as structural Verilog: 23 circuits, main circuit workplace_F3_4
module workplace_F3_4 (
  input  in_1,
  input  in_2,
  input  in_3,
  input  A0,
  input  B0,
  input  Ci0,
  input  A1,
  input  B1,
  input  A2,
  input  B2,
  input  A3,
  input  B3,
  input  in_13,
  input  in_14,
  input  in_15,
  input  in_16,
  input  in_17,
  input  in_18,
  input  in_19,
  input  in_20,
  input  in_21,
  input  in_22,
  input  in_23,
  input  in_24,
  input  in_25,
  input  in_26,
  input  in_27,
  input  in_28,
  input  in_29,
  output out_30,
  output out_31,
  output C0,
  output C1,
  output C2,
  output C3,
  output Co,
  output out_37,
  output out_38,
  output out_39,
  output out_40,
  output out_41,
  output out_42,
  output out_43,
  output out_44,
  output out_45
);

  wire and_1_out, and_2_out, and_3_out, and_4_out, and_5_out, and_6_out, and_7_out, and_8_out, and_9_out,
       and_10_out, decoder_7_segments_0_9_1_sa, decoder_7_segments_0_9_1_sb, decoder_7_segments_0_9_1_sc,
       decoder_7_segments_0_9_1_sd, decoder_7_segments_0_9_1_se, decoder_7_segments_0_9_1_sf,
       decoder_7_segments_0_9_1_sg, decoder_7_segments_0_9_1_sh, decoder_7_segments_0_9_2_sa,
       decoder_7_segments_0_9_2_sb, decoder_7_segments_0_9_2_sc, decoder_7_segments_0_9_2_sd,
       decoder_7_segments_0_9_2_se, decoder_7_segments_0_9_2_sf, decoder_7_segments_0_9_2_sg,
       decoder_7_segments_0_9_2_sh, decoder_7_segments_1_sa, decoder_7_segments_1_sb,
       decoder_7_segments_1_sc, decoder_7_segments_1_sd, decoder_7_segments_1_se, decoder_7_segments_1_sf,
       decoder_7_segments_1_sg, decoder_7_segments_1_sh, decoder_7_segments_2_sa, decoder_7_segments_2_sb,
       decoder_7_segments_2_sc, decoder_7_segments_2_sd, decoder_7_segments_2_se, decoder_7_segments_2_sf,
       decoder_7_segments_2_sg, decoder_7_segments_2_sh, decoder_7_segments_3_sa, decoder_7_segments_3_sb,
       decoder_7_segments_3_sc, decoder_7_segments_3_sd, decoder_7_segments_3_se, decoder_7_segments_3_sf,
       decoder_7_segments_3_sg, decoder_7_segments_3_sh, decoder_7_segments_4_sa, decoder_7_segments_4_sb,
       decoder_7_segments_4_sc, decoder_7_segments_4_sd, decoder_7_segments_4_se, decoder_7_segments_4_sf,
       decoder_7_segments_4_sg, decoder_7_segments_4_sh, decoder_7_segments_5_sa, decoder_7_segments_5_sb,
       decoder_7_segments_5_sc, decoder_7_segments_5_sd, decoder_7_segments_5_se, decoder_7_segments_5_sf,
       decoder_7_segments_5_sg, decoder_7_segments_5_sh, decoder_7_segments_6_sa, decoder_7_segments_6_sb,
       decoder_7_segments_6_sc, decoder_7_segments_6_sd, decoder_7_segments_6_se, decoder_7_segments_6_sf,
       decoder_7_segments_6_sg, decoder_7_segments_6_sh, decoder_7_segments_7_sa, decoder_7_segments_7_sb,
       decoder_7_segments_7_sc, decoder_7_segments_7_sd, decoder_7_segments_7_se, decoder_7_segments_7_sf,
       decoder_7_segments_7_sg, decoder_7_segments_7_sh, decoder_7_segments_8_sa, decoder_7_segments_8_sb,
       decoder_7_segments_8_sc, decoder_7_segments_8_sd, decoder_7_segments_8_se, decoder_7_segments_8_sf,
       decoder_7_segments_8_sg, decoder_7_segments_8_sh, decoder_7_segments_9_sa, decoder_7_segments_9_sb,
       decoder_7_segments_9_sc, decoder_7_segments_9_sd, decoder_7_segments_9_se, decoder_7_segments_9_sf,
       decoder_7_segments_9_sg, decoder_7_segments_9_sh, decoder_7_segments_10_sa, decoder_7_segments_10_sb,
       decoder_7_segments_10_sc, decoder_7_segments_10_sd, decoder_7_segments_10_se,
       decoder_7_segments_10_sf, decoder_7_segments_10_sg, decoder_7_segments_10_sh,
       decoder_7_segments_11_sa, decoder_7_segments_11_sb, decoder_7_segments_11_sc,
       decoder_7_segments_11_sd, decoder_7_segments_11_se, decoder_7_segments_11_sf,
       decoder_7_segments_11_sg, decoder_7_segments_11_sh, decoder_7_segments_12_sa,
       decoder_7_segments_12_sb, decoder_7_segments_12_sc, decoder_7_segments_12_sd,
       decoder_7_segments_12_se, decoder_7_segments_12_sf, decoder_7_segments_12_sg,
       decoder_7_segments_12_sh, dipswitch_1_p1, dipswitch_1_p2, dipswitch_1_p3, dipswitch_1_p4,
       dipswitch_1_p5, dipswitch_2_p1, dipswitch_2_p2, dipswitch_2_p3, dipswitch_2_p4, dipswitch_3_p1,
       dipswitch_3_p2, dipswitch_3_p3, dipswitch_3_p4, dipswitch_3_p5, dipswitch_3_p6, dipswitch_3_p7,
       dipswitch_3_p8, dipswitch_4_p1, dipswitch_4_p2, dipswitch_4_p3, dipswitch_4_p4, dipswitch_4_p5,
       dipswitch_4_p6, dipswitch_4_p7, dipswitch_4_p8, dipswitch_5_p1, dipswitch_5_p2, dipswitch_5_p3,
       dipswitch_5_p4, encoder_16_4_1_y0, encoder_16_4_1_y1, encoder_16_4_1_y2, encoder_16_4_1_y3,
       full_adder_1_1_co, full_adder_1_2_co, full_adder_1_3_co, half_adder_1_1_c, half_adder_1_1_s,
       not_1_out, not_2_out, not_3_out, not_4_out, selector_2_1_1_y, selector_2_1_2_y, selector_2_1_3_y,
       selector_2_1_4_y, selector_2_1_5_y, selector_2_1_6_y, selector_2_1_7_y, selector_2_1_8_y;

  // DipSwitch #(.number(5)) dipswitch_1: pin names not known; wires that end beside it: dipswitch_1_p1, dipswitch_1_p2, dipswitch_1_p3, dipswitch_1_p4, dipswitch_1_p5
  // DipSwitch #(.number(4)) dipswitch_2: pin names not known; wires that end beside it: dipswitch_2_p1, dipswitch_2_p2, dipswitch_2_p3, dipswitch_2_p4
  // DipSwitch dipswitch_3: pin names not known; wires that end beside it: dipswitch_3_p1, dipswitch_3_p2, dipswitch_3_p3, dipswitch_3_p4, dipswitch_3_p5, dipswitch_3_p6, dipswitch_3_p7, dipswitch_3_p8
  // DipSwitch dipswitch_4: pin names not known; wires that end beside it: dipswitch_4_p1, dipswitch_4_p2, dipswitch_4_p3, dipswitch_4_p4, dipswitch_4_p5, dipswitch_4_p6, dipswitch_4_p7, dipswitch_4_p8
  not not_1 (not_1_out, dipswitch_1_p5);
  not not_2 (not_2_out, dipswitch_1_p5);
  not not_3 (not_3_out, dipswitch_1_p5);
  not not_4 (not_4_out, dipswitch_1_p5);
  _7_Segment_Display u_7_segment_display_1 (.g(in_28));  // open: f, a, b, e, d, c, dp
  _7_Segment_Display u_7_segment_display_2 (
    .g(decoder_7_segments_5_sg), .f(decoder_7_segments_5_sf), .a(decoder_7_segments_5_sa),
    .b(decoder_7_segments_5_sb), .e(decoder_7_segments_5_se), .d(decoder_7_segments_5_sd),
    .c(decoder_7_segments_5_sc), .dp(decoder_7_segments_5_sh));
  _7_Segment_Display u_7_segment_display_3 (.g(in_29));  // open: f, a, b, e, d, c, dp
  _7_Segment_Display u_7_segment_display_4 (
    .g(decoder_7_segments_6_sg), .f(decoder_7_segments_6_sf), .a(decoder_7_segments_6_sa),
    .b(decoder_7_segments_6_sb), .e(decoder_7_segments_6_se), .d(decoder_7_segments_6_sd),
    .c(decoder_7_segments_6_sc), .dp(decoder_7_segments_6_sh));
  and and_1 (and_1_out, dipswitch_1_p1, dipswitch_1_p5);
  and and_2 (and_2_out, dipswitch_1_p2, dipswitch_1_p5);
  and and_3 (and_3_out, dipswitch_1_p3, dipswitch_1_p5);
  and and_4 (and_4_out, dipswitch_1_p4, dipswitch_1_p5);
  and and_5 (and_5_out, dipswitch_1_p1, not_1_out);
  and and_6 (and_6_out, dipswitch_1_p2, not_2_out);
  and and_7 (and_7_out, dipswitch_1_p3, not_3_out);
  and and_8 (and_8_out, dipswitch_1_p4, not_4_out);
  half_adder_1 half_adder_1_1 (.A(in_1), .B(in_2), .S(half_adder_1_1_s), .C(half_adder_1_1_c));
  decoder_7_segments decoder_7_segments_1 (
    .I3(A3), .I2(A2), .I1(A1), .I0(A0), .SA(decoder_7_segments_1_sa), .SB(decoder_7_segments_1_sb),
    .SC(decoder_7_segments_1_sc), .SD(decoder_7_segments_1_sd), .SE(decoder_7_segments_1_se),
    .SF(decoder_7_segments_1_sf), .SG(decoder_7_segments_1_sg), .SH(decoder_7_segments_1_sh));
  decoder_7_segments decoder_7_segments_2 (
    .I3(B3), .I2(B2), .I1(B1), .I0(B0), .SA(decoder_7_segments_2_sa), .SB(decoder_7_segments_2_sb),
    .SC(decoder_7_segments_2_sc), .SD(decoder_7_segments_2_sd), .SE(decoder_7_segments_2_se),
    .SF(decoder_7_segments_2_sf), .SG(decoder_7_segments_2_sg), .SH(decoder_7_segments_2_sh));
  decoder_7_segments decoder_7_segments_3 (
    .I3(in_20), .I2(in_18), .I1(in_16), .I0(in_13), .SA(decoder_7_segments_3_sa),
    .SB(decoder_7_segments_3_sb), .SC(decoder_7_segments_3_sc), .SD(decoder_7_segments_3_sd),
    .SE(decoder_7_segments_3_se), .SF(decoder_7_segments_3_sf), .SG(decoder_7_segments_3_sg),
    .SH(decoder_7_segments_3_sh));
  decoder_7_segments decoder_7_segments_4 (
    .I3(in_21), .I2(in_19), .I1(in_17), .I0(in_14), .SA(decoder_7_segments_4_sa),
    .SB(decoder_7_segments_4_sb), .SC(decoder_7_segments_4_sc), .SD(decoder_7_segments_4_sd),
    .SE(decoder_7_segments_4_se), .SF(decoder_7_segments_4_sf), .SG(decoder_7_segments_4_sg),
    .SH(decoder_7_segments_4_sh));
  decoder_7_segments decoder_7_segments_5 (
    .I2(in_26), .I1(in_24), .I0(in_22), .SA(decoder_7_segments_5_sa), .SB(decoder_7_segments_5_sb),
    .SC(decoder_7_segments_5_sc), .SD(decoder_7_segments_5_sd), .SE(decoder_7_segments_5_se),
    .SF(decoder_7_segments_5_sf), .SG(decoder_7_segments_5_sg), .SH(decoder_7_segments_5_sh));  // open: I3
  decoder_7_segments decoder_7_segments_6 (
    .I2(in_27), .I1(in_25), .I0(in_23), .SA(decoder_7_segments_6_sa), .SB(decoder_7_segments_6_sb),
    .SC(decoder_7_segments_6_sc), .SD(decoder_7_segments_6_sd), .SE(decoder_7_segments_6_se),
    .SF(decoder_7_segments_6_sf), .SG(decoder_7_segments_6_sg), .SH(decoder_7_segments_6_sh));  // open: I3
  decoder_7_segments_0_9 decoder_7_segments_0_9_1 (
    .I3(dipswitch_2_p1), .I2(dipswitch_2_p2), .I1(dipswitch_2_p3), .I0(dipswitch_2_p4),
    .SA(decoder_7_segments_0_9_1_sa), .SB(decoder_7_segments_0_9_1_sb), .SC(decoder_7_segments_0_9_1_sc),
    .SD(decoder_7_segments_0_9_1_sd), .SE(decoder_7_segments_0_9_1_se), .SF(decoder_7_segments_0_9_1_sf),
    .SG(decoder_7_segments_0_9_1_sg), .SH(decoder_7_segments_0_9_1_sh));
  encoder_16_4 encoder_16_4_1 (
    .I0(dipswitch_3_p1), .I1(dipswitch_3_p2), .I2(dipswitch_3_p3), .I3(dipswitch_3_p4), .I4(dipswitch_3_p5),
    .I5(dipswitch_3_p6), .I6(dipswitch_3_p7), .I7(dipswitch_3_p8), .I8(dipswitch_4_p1), .I9(dipswitch_4_p2),
    .I10(dipswitch_4_p3), .I11(dipswitch_4_p4), .I12(dipswitch_4_p5), .I13(dipswitch_4_p6),
    .I14(dipswitch_4_p7), .I15(dipswitch_4_p8), .Y0(encoder_16_4_1_y0), .Y1(encoder_16_4_1_y1),
    .Y2(encoder_16_4_1_y2), .Y3(encoder_16_4_1_y3));
  and and_9 (and_9_out, in_1, in_3);
  and and_10 (and_10_out, in_2, in_3);
  _7_Segment_Display u_7_segment_display_5 (
    .g(decoder_7_segments_1_sg), .f(decoder_7_segments_1_sf), .a(decoder_7_segments_1_sa),
    .b(decoder_7_segments_1_sb), .e(decoder_7_segments_1_se), .d(decoder_7_segments_1_sd),
    .c(decoder_7_segments_1_sc), .dp(decoder_7_segments_1_sh));
  _7_Segment_Display u_7_segment_display_6 (
    .g(decoder_7_segments_2_sg), .f(decoder_7_segments_2_sf), .a(decoder_7_segments_2_sa),
    .b(decoder_7_segments_2_sb), .e(decoder_7_segments_2_se), .d(decoder_7_segments_2_sd),
    .c(decoder_7_segments_2_sc), .dp(decoder_7_segments_2_sh));
  _7_Segment_Display u_7_segment_display_7 (
    .g(decoder_7_segments_3_sg), .f(decoder_7_segments_3_sf), .a(decoder_7_segments_3_sa),
    .b(decoder_7_segments_3_sb), .e(decoder_7_segments_3_se), .d(decoder_7_segments_3_sd),
    .c(decoder_7_segments_3_sc), .dp(decoder_7_segments_3_sh));
  _7_Segment_Display u_7_segment_display_8 (
    .g(decoder_7_segments_4_sg), .f(decoder_7_segments_4_sf), .a(decoder_7_segments_4_sa),
    .b(decoder_7_segments_4_sb), .e(decoder_7_segments_4_se), .d(decoder_7_segments_4_sd),
    .c(decoder_7_segments_4_sc), .dp(decoder_7_segments_4_sh));
  decoder_7_segments decoder_7_segments_7 (
    .I3(and_1_out), .I2(and_2_out), .I1(and_3_out), .I0(and_4_out), .SA(decoder_7_segments_7_sa),
    .SB(decoder_7_segments_7_sb), .SC(decoder_7_segments_7_sc), .SD(decoder_7_segments_7_sd),
    .SE(decoder_7_segments_7_se), .SF(decoder_7_segments_7_sf), .SG(decoder_7_segments_7_sg),
    .SH(decoder_7_segments_7_sh));
  decoder_7_segments_0_9 decoder_7_segments_0_9_2 (
    .I3(and_5_out), .I2(and_6_out), .I1(and_7_out), .I0(and_8_out), .SA(decoder_7_segments_0_9_2_sa),
    .SB(decoder_7_segments_0_9_2_sb), .SC(decoder_7_segments_0_9_2_sc), .SD(decoder_7_segments_0_9_2_sd),
    .SE(decoder_7_segments_0_9_2_se), .SF(decoder_7_segments_0_9_2_sf), .SG(decoder_7_segments_0_9_2_sg),
    .SH(decoder_7_segments_0_9_2_sh));
  or or_1 (out_31, half_adder_1_1_c, and_9_out, and_10_out);
  _7_Segment_Display u_7_segment_display_9 (
    .g(decoder_7_segments_0_9_1_sg), .f(decoder_7_segments_0_9_1_sf), .a(decoder_7_segments_0_9_1_sa),
    .b(decoder_7_segments_0_9_1_sb), .e(decoder_7_segments_0_9_1_se), .d(decoder_7_segments_0_9_1_sd),
    .c(decoder_7_segments_0_9_1_sc), .dp(decoder_7_segments_0_9_1_sh));
  half_adder_1 half_adder_1_2 (.A(half_adder_1_1_s), .B(in_3), .S(out_30));  // open: C
  // DipSwitch #(.number(4)) dipswitch_5: pin names not known; wires that end beside it: dipswitch_5_p1, dipswitch_5_p2, dipswitch_5_p3, dipswitch_5_p4
  decoder_7_segments decoder_7_segments_8 (
    .I3(encoder_16_4_1_y3), .I2(encoder_16_4_1_y2), .I1(encoder_16_4_1_y1), .I0(encoder_16_4_1_y0),
    .SA(decoder_7_segments_8_sa), .SB(decoder_7_segments_8_sb), .SC(decoder_7_segments_8_sc),
    .SD(decoder_7_segments_8_sd), .SE(decoder_7_segments_8_se), .SF(decoder_7_segments_8_sf),
    .SG(decoder_7_segments_8_sg), .SH(decoder_7_segments_8_sh));
  sign_magnitude_adder_4 sign_magnitude_adder_4_1 (
    .A0(in_22), .B0(in_23), .A1(in_24), .B1(in_25), .A2(in_26), .B2(in_27), .A3(in_28), .B3(in_29),
    .R0(out_42), .R1(out_43), .R2(out_44), .R3(out_45));
  _7_Segment_Display u_7_segment_display_10 (
    .g(decoder_7_segments_8_sg), .f(decoder_7_segments_8_sf), .a(decoder_7_segments_8_sa),
    .b(decoder_7_segments_8_sb), .e(decoder_7_segments_8_se), .d(decoder_7_segments_8_sd),
    .c(decoder_7_segments_8_sc), .dp(decoder_7_segments_8_sh));
  full_adder_1 full_adder_1_1 (.A(A0), .B(B0), .Ci(Ci0), .S(C0), .Co(full_adder_1_1_co));
  full_adder_1 full_adder_1_2 (.A(A1), .B(B1), .Ci(full_adder_1_1_co), .S(C1), .Co(full_adder_1_2_co));
  full_adder_1 full_adder_1_3 (.A(A2), .B(B2), .Ci(full_adder_1_2_co), .S(C2), .Co(full_adder_1_3_co));
  full_adder_1 full_adder_1_4 (.A(A3), .B(B3), .Ci(full_adder_1_3_co), .S(C3), .Co(Co));
  _7_Segment_Display u_7_segment_display_11 (.g(out_45));  // open: f, a, b, e, d, c, dp
  selector_2_1 selector_2_1_1 (
    .D0(decoder_7_segments_0_9_2_sa), .S(dipswitch_1_p5), .D1(decoder_7_segments_7_sa), .Y(selector_2_1_1_y));
  selector_2_1 selector_2_1_2 (
    .D0(decoder_7_segments_0_9_2_sb), .S(dipswitch_1_p5), .D1(decoder_7_segments_7_sb), .Y(selector_2_1_2_y));
  selector_2_1 selector_2_1_3 (
    .D0(decoder_7_segments_0_9_2_sc), .S(dipswitch_1_p5), .D1(decoder_7_segments_7_sc), .Y(selector_2_1_3_y));
  selector_2_1 selector_2_1_4 (
    .D0(decoder_7_segments_0_9_2_sd), .S(dipswitch_1_p5), .D1(decoder_7_segments_7_sd), .Y(selector_2_1_4_y));
  selector_2_1 selector_2_1_5 (
    .D0(decoder_7_segments_0_9_2_se), .S(dipswitch_1_p5), .D1(decoder_7_segments_7_se), .Y(selector_2_1_5_y));
  selector_2_1 selector_2_1_6 (
    .D0(decoder_7_segments_0_9_2_sf), .S(dipswitch_1_p5), .D1(decoder_7_segments_7_sf), .Y(selector_2_1_6_y));
  selector_2_1 selector_2_1_7 (
    .D0(decoder_7_segments_0_9_2_sg), .S(dipswitch_1_p5), .D1(decoder_7_segments_7_sg), .Y(selector_2_1_7_y));
  selector_2_1 selector_2_1_8 (
    .D0(decoder_7_segments_0_9_2_sh), .S(dipswitch_1_p5), .D1(decoder_7_segments_7_sh), .Y(selector_2_1_8_y));
  full_subtractor_4 full_subtractor_4_1 (
    .A0(in_13), .B0(in_14), .Bi(in_15), .A1(in_16), .B1(in_17), .A2(in_18), .B2(in_19), .A3(in_20),
    .B3(in_21), .D0(out_37), .D1(out_38), .D2(out_39), .D3(out_40), .Bo(out_41));
  _7_Segment_Display u_7_segment_display_12 (
    .g(decoder_7_segments_10_sg), .f(decoder_7_segments_10_sf), .a(decoder_7_segments_10_sa),
    .b(decoder_7_segments_10_sb), .e(decoder_7_segments_10_se), .d(decoder_7_segments_10_sd),
    .c(decoder_7_segments_10_sc), .dp(decoder_7_segments_10_sh));
  decoder_7_segments decoder_7_segments_9 (
    .I3(dipswitch_5_p1), .I2(dipswitch_5_p2), .I1(dipswitch_5_p3), .I0(dipswitch_5_p4),
    .SA(decoder_7_segments_9_sa), .SB(decoder_7_segments_9_sb), .SC(decoder_7_segments_9_sc),
    .SD(decoder_7_segments_9_sd), .SE(decoder_7_segments_9_se), .SF(decoder_7_segments_9_sf),
    .SG(decoder_7_segments_9_sg), .SH(decoder_7_segments_9_sh));
  _7_Segment_Display u_7_segment_display_13 (
    .g(selector_2_1_7_y), .f(selector_2_1_6_y), .a(selector_2_1_1_y), .b(selector_2_1_2_y),
    .e(selector_2_1_5_y), .d(selector_2_1_4_y), .c(selector_2_1_3_y), .dp(selector_2_1_8_y));
  decoder_7_segments decoder_7_segments_10 (
    .I2(out_44), .I1(out_43), .I0(out_42), .SA(decoder_7_segments_10_sa), .SB(decoder_7_segments_10_sb),
    .SC(decoder_7_segments_10_sc), .SD(decoder_7_segments_10_sd), .SE(decoder_7_segments_10_se),
    .SF(decoder_7_segments_10_sf), .SG(decoder_7_segments_10_sg), .SH(decoder_7_segments_10_sh));  // open: I3
  _7_Segment_Display u_7_segment_display_14 (
    .g(decoder_7_segments_9_sg), .f(decoder_7_segments_9_sf), .a(decoder_7_segments_9_sa),
    .b(decoder_7_segments_9_sb), .e(decoder_7_segments_9_se), .d(decoder_7_segments_9_sd),
    .c(decoder_7_segments_9_sc), .dp(decoder_7_segments_9_sh));
  decoder_7_segments decoder_7_segments_11 (
    .I3(C3), .I2(C2), .I1(C1), .I0(C0), .SA(decoder_7_segments_11_sa), .SB(decoder_7_segments_11_sb),
    .SC(decoder_7_segments_11_sc), .SD(decoder_7_segments_11_sd), .SE(decoder_7_segments_11_se),
    .SF(decoder_7_segments_11_sf), .SG(decoder_7_segments_11_sg), .SH(decoder_7_segments_11_sh));
  _7_Segment_Display u_7_segment_display_15 (
    .g(decoder_7_segments_11_sg), .f(decoder_7_segments_11_sf), .a(decoder_7_segments_11_sa),
    .b(decoder_7_segments_11_sb), .e(decoder_7_segments_11_se), .d(decoder_7_segments_11_sd),
    .c(decoder_7_segments_11_sc), .dp(decoder_7_segments_11_sh));
  LED led_1 (.in(Co));
  decoder_7_segments decoder_7_segments_12 (
    .I3(out_40), .I2(out_39), .I1(out_38), .I0(out_37), .SA(decoder_7_segments_12_sa),
    .SB(decoder_7_segments_12_sb), .SC(decoder_7_segments_12_sc), .SD(decoder_7_segments_12_sd),
    .SE(decoder_7_segments_12_se), .SF(decoder_7_segments_12_sf), .SG(decoder_7_segments_12_sg),
    .SH(decoder_7_segments_12_sh));
  _7_Segment_Display u_7_segment_display_16 (
    .g(decoder_7_segments_12_sg), .f(decoder_7_segments_12_sf), .a(decoder_7_segments_12_sa),
    .b(decoder_7_segments_12_sb), .e(decoder_7_segments_12_se), .d(decoder_7_segments_12_sd),
    .c(decoder_7_segments_12_sc), .dp(decoder_7_segments_12_sh));
  LED led_2 (.in(out_41));
endmodule

module decoder_2_4 (
  input  A1,
  input  A0,
  output Y0,
  output Y1,
  output Y2,
  output Y3
);

  wire not_1_out, not_2_out;

  not not_1 (not_1_out, A1);
  not not_2 (not_2_out, A0);
  and and_1 (Y0, not_1_out, not_2_out);
  and and_2 (Y1, not_1_out, A0);
  and and_3 (Y2, A1, not_2_out);
  and and_4 (Y3, A1, A0);
endmodule

module decoder_3_8 (
  input  A2,
  input  A1,
  input  A0,
  output Y0,
  output Y1,
  output Y2,
  output Y3,
  output Y4,
  output Y5,
  output Y6,
  output Y7
);

  wire decoder_2_4_1_y0, decoder_2_4_1_y1, decoder_2_4_1_y2, decoder_2_4_1_y3, decoder_2_4_2_y0,
       decoder_2_4_2_y1, decoder_2_4_2_y2, decoder_2_4_2_y3;

  decoder_2_4 decoder_2_4_1 (
    .A1(A2), .A0(A1), .Y0(decoder_2_4_1_y0), .Y1(decoder_2_4_1_y1), .Y2(decoder_2_4_1_y2),
    .Y3(decoder_2_4_1_y3));
  decoder_2_4 decoder_2_4_2 (
    .A1(A1), .A0(A0), .Y0(decoder_2_4_2_y0), .Y1(decoder_2_4_2_y1), .Y2(decoder_2_4_2_y2),
    .Y3(decoder_2_4_2_y3));
  and and_1 (Y0, decoder_2_4_1_y0, decoder_2_4_2_y0);
  and and_2 (Y1, decoder_2_4_1_y0, decoder_2_4_2_y1);
  and and_3 (Y2, decoder_2_4_1_y1, decoder_2_4_2_y2);
  and and_4 (Y3, decoder_2_4_1_y1, decoder_2_4_2_y3);
  and and_5 (Y4, decoder_2_4_1_y2, decoder_2_4_2_y0);
  and and_6 (Y5, decoder_2_4_1_y2, decoder_2_4_2_y1);
  and and_7 (Y6, decoder_2_4_1_y3, decoder_2_4_2_y2);
  and and_8 (Y7, decoder_2_4_1_y3, decoder_2_4_2_y3);
endmodule

module decoder_7_segments (
  input  I3,
  input  I2,
  input  I1,
  input  I0,
  output SA,
  output SB,
  output SC,
  output SD,
  output SE,
  output SF,
  output SG,
  output SH
);

  wire M0_out, M1_out, M2_out, M3_out, M4_out, M5_out, M6_out, M7_out, M9_out, M10_out, M11_out, M12_out,
       M13_out, M14_out, M15_out, not_1_out, not_2_out, not_3_out, not_4_out;

  not not_1 (not_1_out, I3);
  not not_2 (not_2_out, I2);
  not not_3 (not_3_out, I1);
  not not_4 (not_4_out, I0);
  or M0 (M0_out, I3, I2, I1, I0);
  or M1 (M1_out, I3, I2, I1, not_4_out);
  or M2 (M2_out, I3, I2, not_3_out, I0);
  or M3 (M3_out, I3, I2, not_3_out, not_4_out);
  or M4 (M4_out, I3, not_2_out, I1, I0);
  or M5 (M5_out, I3, not_2_out, I1, not_4_out);
  or M6 (M6_out, I3, not_2_out, not_3_out, I0);
  or M7 (M7_out, I3, not_2_out, not_3_out, not_4_out);
  or M9 (M9_out, not_1_out, I2, I1, not_4_out);
  or M10 (M10_out, not_1_out, I2, not_3_out, I0);
  or M11 (M11_out, not_1_out, I2, not_3_out, not_4_out);
  or M12 (M12_out, not_1_out, not_2_out, I1, I0);
  or M13 (M13_out, not_1_out, not_2_out, I1, not_4_out);
  or M14 (M14_out, not_1_out, not_2_out, not_3_out, I0);
  or M15 (M15_out, not_1_out, not_2_out, not_3_out, not_4_out);
  and A (SA, M1_out, M4_out, M11_out, M13_out);
  and B (SB, M5_out, M6_out, M11_out, M12_out, M14_out, M15_out);
  and C (SC, M2_out, M12_out, M14_out, M15_out);
  and D (SD, M1_out, M4_out, M7_out, M10_out, M15_out);
  and E (SE, M1_out, M3_out, M4_out, M5_out, M7_out, M9_out);
  and F (SF, M1_out, M2_out, M3_out, M7_out, M13_out);
  and G (SG, M0_out, M1_out, M7_out, M12_out);

  assign SH = 1'b0;
endmodule

module decoder_7_segments_0_9 (
  input  I3,
  input  I2,
  input  I1,
  input  I0,
  output SA,
  output SB,
  output SC,
  output SD,
  output SE,
  output SF,
  output SG,
  output SH
);

  wire and_1_out, M0_out, M1_out, M2_out, M3_out, M4_out, M5_out, M6_out, M7_out, M8_out, M9_out, M10_out,
       M11_out, M12_out, M13_out, M14_out, M15_out, not_1_out, not_2_out, not_3_out, not_4_out;

  not not_1 (not_1_out, I3);
  not not_2 (not_2_out, I2);
  not not_3 (not_3_out, I1);
  not not_4 (not_4_out, I0);
  or M0 (M0_out, I3, I2, I1, I0);
  or M1 (M1_out, I3, I2, I1, not_4_out);
  or M2 (M2_out, I3, I2, not_3_out, I0);
  or M3 (M3_out, I3, I2, not_3_out, not_4_out);
  or M4 (M4_out, I3, not_2_out, I1, I0);
  or M5 (M5_out, I3, not_2_out, I1, not_4_out);
  or M6 (M6_out, I3, not_2_out, not_3_out, I0);
  or M7 (M7_out, I3, not_2_out, not_3_out, not_4_out);
  or M9 (M9_out, not_1_out, I2, I1, not_4_out);
  or M10 (M10_out, not_1_out, I2, not_3_out, I0);
  or M11 (M11_out, not_1_out, I2, not_3_out, not_4_out);
  or M12 (M12_out, not_1_out, not_2_out, I1, I0);
  or M13 (M13_out, not_1_out, not_2_out, I1, not_4_out);
  or M14 (M14_out, not_1_out, not_2_out, not_3_out, I0);
  or M15 (M15_out, not_1_out, not_2_out, not_3_out, not_4_out);
  or M8 (M8_out, not_1_out, I2, I1, I0);
  and and_1 (and_1_out, M10_out, M11_out, M12_out, M13_out, M14_out, M15_out);
  and and_2 (SA, M1_out, M4_out, and_1_out);
  and and_3 (SB, M5_out, M6_out, and_1_out);
  and and_4 (SC, M2_out, and_1_out);
  and and_5 (SD, M1_out, M4_out, M7_out, and_1_out);
  and and_6 (SE, M1_out, M3_out, M4_out, M5_out, M7_out, and_1_out, M9_out);
  and and_7 (SF, M1_out, M2_out, M3_out, M7_out, and_1_out);
  and and_8 (SG, M0_out, M1_out, M7_out, and_1_out);
  and and_9 (SH, M0_out, M1_out, M2_out, M3_out, M4_out, M5_out, M6_out, M7_out, M8_out, M9_out);
endmodule

module encoder_16_4 (
  input  I0,
  input  I1,
  input  I2,
  input  I3,
  input  I4,
  input  I5,
  input  I6,
  input  I7,
  input  I8,
  input  I9,
  input  I10,
  input  I11,
  input  I12,
  input  I13,
  input  I14,
  input  I15,
  output Y0,
  output Y1,
  output Y2,
  output Y3
);

  wire or_1_out, or_2_out, or_3_out, or_4_out, or_5_out, or_6_out, or_7_out, or_8_out;

  or or_1 (or_1_out, I1, I3, I5, I7);
  or or_2 (or_2_out, I9, I11, I13, I15);
  or or_3 (or_3_out, I2, I3, I6, I7);
  or or_4 (or_4_out, I10, I11, I14, I15);
  or or_5 (or_5_out, I4, I5, I6, I7);
  or or_6 (or_6_out, I12, I13, I14, I15);
  or or_7 (or_7_out, I8, I9, I10, I11);
  or or_8 (or_8_out, I12, I13, I14, I15);
  or or_9 (Y0, or_1_out, or_2_out);
  or or_10 (Y1, or_3_out, or_4_out);
  or or_11 (Y2, or_5_out, or_6_out);
  or or_12 (Y3, or_7_out, or_8_out);
endmodule

module encoder_pr_4_2 (
  input  I3,
  input  I2,
  input  I1,
  input  I0,
  output Y1,
  output Y0
);

  wire and_1_out, not_1_out;

  not not_1 (not_1_out, I2);
  or or_1 (Y1, I3, I2);
  and and_1 (and_1_out, not_1_out, I1);
  or or_2 (Y0, I3, and_1_out);
endmodule

module encoder_4_2 (
  input  I3,
  input  I2,
  input  I1,
  input  I0,
  output Y1,
  output Y0
);

  or or_1 (Y1, I3, I2);
  or or_2 (Y0, I1, I3);
endmodule

module selector_2_1 (
  input  D0,
  input  S,
  input  D1,
  output Y
);

  wire and_1_out, and_2_out, not_1_out;

  not not_1 (not_1_out, S);
  and and_1 (and_1_out, D0, not_1_out);
  and and_2 (and_2_out, S, D1);
  or or_1 (Y, and_1_out, and_2_out);
endmodule

module selector_4_1 (
  input  D3,
  input  D2,
  input  D1,
  input  D0,
  input  S1,
  input  S0,
  output Y
);

  wire and_1_out, and_2_out, and_3_out, and_4_out, not_1_out, not_2_out;

  not not_1 (not_1_out, S1);
  not not_2 (not_2_out, S0);
  and and_1 (and_1_out, not_1_out, not_2_out, D0);
  and and_2 (and_2_out, not_1_out, S0, D1);
  and and_3 (and_3_out, S1, not_2_out, D2);
  and and_4 (and_4_out, S1, D3, S0);
  or or_1 (Y, and_1_out, and_2_out, and_3_out, and_4_out);
endmodule

module selector_4_1_3bits (
  input  [2:0] D3,
  input  [2:0] D2,
  input  [2:0] D1,
  input  [2:0] D0,
  input  S1,
  input  S0,
  output [2:0] Y
);

  selector_4_1 selector_4_1_1 (.D3(D3[2]), .D2(D2[2]), .D1(D1[2]), .D0(D0[2]), .S1(S1), .S0(S0), .Y(Y[2]));
  selector_4_1 selector_4_1_2 (.D3(D3[1]), .D2(D2[1]), .D1(D1[1]), .D0(D0[1]), .S1(S1), .S0(S0), .Y(Y[1]));
  selector_4_1 selector_4_1_3 (.D3(D3[0]), .D2(D2[0]), .D1(D1[0]), .D0(D0[0]), .S1(S1), .S0(S0), .Y(Y[0]));
endmodule

module comparator_4 (
  input  A0,
  input  B0,
  input  A1,
  input  B1,
  input  A2,
  input  B2,
  input  A3,
  input  B3,
  output Y
);

  wire not_1_out, not_2_out, not_3_out, not_4_out, xor_1_out, xor_2_out, xor_3_out, xor_4_out;

  xor xor_1 (xor_1_out, A0, B0);
  xor xor_2 (xor_2_out, A1, B1);
  xor xor_3 (xor_3_out, A2, B2);
  xor xor_4 (xor_4_out, A3, B3);
  not not_1 (not_1_out, xor_1_out);
  not not_2 (not_2_out, xor_2_out);
  not not_3 (not_3_out, xor_3_out);
  not not_4 (not_4_out, xor_4_out);
  and and_1 (Y, not_1_out, not_2_out, not_3_out, not_4_out);
  LED led_1 (.in(Y));
endmodule

module full_adder_1 (
  input  A,
  input  B,
  input  Ci,
  output S,
  output Co
);

  wire and_1_out, and_2_out, and_3_out, xor_1_out;

  xor xor_1 (xor_1_out, A, B);
  and and_1 (and_1_out, A, B);
  and and_2 (and_2_out, A, Ci);
  and and_3 (and_3_out, B, Ci);
  xor xor_2 (S, xor_1_out, Ci);
  or or_1 (Co, and_1_out, and_2_out, and_3_out);
endmodule

module half_adder_1 (
  input  A,
  input  B,
  output S,
  output C
);

  xor xor_1 (S, A, B);
  and and_1 (C, A, B);
endmodule

module full_adder_4 (
  input  A0,
  input  B0,
  input  Ci,
  input  A1,
  input  B1,
  input  A2,
  input  B2,
  input  A3,
  input  B3,
  output C0,
  output C1,
  output C2,
  output C3,
  output Co
);

  wire full_adder_1_1_co, full_adder_1_2_co, full_adder_1_3_co;

  full_adder_1 full_adder_1_1 (.A(A0), .B(B0), .Ci(Ci), .S(C0), .Co(full_adder_1_1_co));
  full_adder_1 full_adder_1_2 (.A(A1), .B(B1), .Ci(full_adder_1_1_co), .S(C1), .Co(full_adder_1_2_co));
  full_adder_1 full_adder_1_3 (.A(A2), .B(B2), .Ci(full_adder_1_2_co), .S(C2), .Co(full_adder_1_3_co));
  full_adder_1 full_adder_1_4 (.A(A3), .B(B3), .Ci(full_adder_1_3_co), .S(C3), .Co(Co));
endmodule

module full_subtractor_1 (
  input  A,
  input  B,
  input  Bi,
  output D,
  output Bo
);

  wire and_1_out, and_2_out, and_3_out, not_1_out, xor_1_out;

  xor xor_1 (xor_1_out, A, B);
  not not_1 (not_1_out, A);
  and and_1 (and_1_out, not_1_out, B);
  and and_2 (and_2_out, not_1_out, Bi);
  and and_3 (and_3_out, B, Bi);
  xor xor_2 (D, xor_1_out, Bi);
  or or_1 (Bo, and_1_out, and_2_out, and_3_out);
endmodule

module full_subtractor_4 (
  input  A0,
  input  B0,
  input  Bi,
  input  A1,
  input  B1,
  input  A2,
  input  B2,
  input  A3,
  input  B3,
  output D0,
  output D1,
  output D2,
  output D3,
  output Bo
);

  wire full_subtractor_1_1_bo, full_subtractor_1_2_bo, full_subtractor_1_3_bo;

  full_subtractor_1 full_subtractor_1_1 (.A(A0), .B(B0), .Bi(Bi), .D(D0), .Bo(full_subtractor_1_1_bo));
  full_subtractor_1 full_subtractor_1_2 (
    .A(A1), .B(B1), .Bi(full_subtractor_1_1_bo), .D(D1), .Bo(full_subtractor_1_2_bo));
  full_subtractor_1 full_subtractor_1_3 (
    .A(A2), .B(B2), .Bi(full_subtractor_1_2_bo), .D(D2), .Bo(full_subtractor_1_3_bo));
  full_subtractor_1 full_subtractor_1_4 (.A(A3), .B(B3), .Bi(full_subtractor_1_3_bo), .D(D3), .Bo(Bo));
endmodule

module sign_magnitude_adder_4 (
  input  A0,
  input  B0,
  input  A1,
  input  B1,
  input  A2,
  input  B2,
  input  A3,
  input  B3,
  output R0,
  output R1,
  output R2,
  output R3
);

  wire and_1_out, and_2_out, and_3_out, and_4_out, and_5_out, and_6_out, and_7_out, and_8_out, and_9_out,
       and_10_out, and_11_out, and_12_out, and_13_out, and_14_out, and_15_out, and_16_out, and_17_out,
       and_18_out, and_19_out, and_20_out, both_plus_or_both_minus_c0, both_plus_or_both_minus_c1,
       both_plus_or_both_minus_c2, both_plus_or_both_minus_co, comparator_4_3_1_y_bigger,
       comparator_4_3_1_y_equal, comparator_4_3_1_y_smaller, full_subtractor_4_1_d0, full_subtractor_4_1_d1,
       full_subtractor_4_1_d2, full_subtractor_4_2_d0, full_subtractor_4_2_d1, full_subtractor_4_2_d2,
       full_subtractor_4_3_d0, full_subtractor_4_3_d1, full_subtractor_4_3_d2, not_1_out, S0_out, S1_out,
       sign1_out, sign2_out, xor_1_out;

  comparator_4_3 comparator_4_3_1 (
    .A3(1'b0), .A2(A2), .B3(1'b0), .B2(B2), .A1(A1), .A0(A0), .B1(B1), .B0(B0),
    .Y_bigger(comparator_4_3_1_y_bigger), .Y_equal(comparator_4_3_1_y_equal),
    .Y_smaller(comparator_4_3_1_y_smaller));
  and and_1 (and_1_out, comparator_4_3_1_y_bigger, A0);
  and and_2 (and_2_out, comparator_4_3_1_y_bigger, B0);
  and and_3 (and_3_out, comparator_4_3_1_y_bigger, A1);
  and and_4 (and_4_out, comparator_4_3_1_y_bigger, B1);
  and and_5 (and_5_out, comparator_4_3_1_y_bigger, A2);
  and and_6 (and_6_out, comparator_4_3_1_y_bigger, B2);
  and and_7 (and_7_out, comparator_4_3_1_y_equal, A0);
  and and_8 (and_8_out, comparator_4_3_1_y_equal, B0);
  and and_9 (and_9_out, comparator_4_3_1_y_equal, A1);
  and and_10 (and_10_out, comparator_4_3_1_y_equal, B1);
  and and_11 (and_11_out, comparator_4_3_1_y_equal, A2);
  and and_12 (and_12_out, comparator_4_3_1_y_equal, B2);
  and and_13 (and_13_out, comparator_4_3_1_y_smaller, B0);
  and and_14 (and_14_out, comparator_4_3_1_y_smaller, A0);
  and and_15 (and_15_out, comparator_4_3_1_y_smaller, B1);
  and and_16 (and_16_out, comparator_4_3_1_y_smaller, A1);
  and and_17 (and_17_out, comparator_4_3_1_y_smaller, B2);
  and and_18 (and_18_out, comparator_4_3_1_y_smaller, A2);
  full_adder_4 both_plus_or_both_minus (
    .A0(A0), .B0(B0), .A1(A1), .B1(B1), .A2(A2), .B2(B2), .A3(A3), .B3(B3), .C0(both_plus_or_both_minus_c0),
    .C1(both_plus_or_both_minus_c1), .C2(both_plus_or_both_minus_c2), .Co(both_plus_or_both_minus_co));  // open: Ci, C3
  full_subtractor_4 full_subtractor_4_1 (
    .A0(and_1_out), .B0(and_2_out), .A1(and_3_out), .B1(and_4_out), .A2(and_5_out), .B2(and_6_out),
    .A3(1'b0), .B3(1'b0), .D0(full_subtractor_4_1_d0), .D1(full_subtractor_4_1_d1),
    .D2(full_subtractor_4_1_d2));  // open: Bi, D3, Bo
  full_subtractor_4 full_subtractor_4_2 (
    .A0(and_7_out), .B0(and_8_out), .A1(and_9_out), .B1(and_10_out), .A2(and_11_out), .B2(and_12_out),
    .A3(1'b0), .B3(1'b0), .D0(full_subtractor_4_2_d0), .D1(full_subtractor_4_2_d1),
    .D2(full_subtractor_4_2_d2));  // open: Bi, D3, Bo
  full_subtractor_4 full_subtractor_4_3 (
    .A0(and_13_out), .B0(and_14_out), .A1(and_15_out), .B1(and_16_out), .A2(and_17_out), .B2(and_18_out),
    .A3(1'b0), .B3(1'b0), .D0(full_subtractor_4_3_d0), .D1(full_subtractor_4_3_d1),
    .D2(full_subtractor_4_3_d2));  // open: Bi, D3, Bo
  and sign1 (sign1_out, A3, comparator_4_3_1_y_bigger);
  and sign2 (sign2_out, comparator_4_3_1_y_smaller, B3);
  not not_1 (not_1_out, comparator_4_3_1_y_bigger);
  xor xor_1 (xor_1_out, B3, A3);
  and S1 (S1_out, not_1_out, xor_1_out);
  and and_19 (and_19_out, comparator_4_3_1_y_bigger, xor_1_out);
  and and_20 (and_20_out, comparator_4_3_1_y_smaller, xor_1_out);
  or S0 (S0_out, and_19_out, and_20_out);
  selector_4_1 selector_4_1_1 (
    .D3(full_subtractor_4_3_d0), .D2(full_subtractor_4_2_d0), .D1(full_subtractor_4_1_d0),
    .D0(both_plus_or_both_minus_c0), .S1(S1_out), .S0(S0_out), .Y(R0));
  selector_4_1 selector_4_1_2 (
    .D3(full_subtractor_4_3_d1), .D2(full_subtractor_4_2_d1), .D1(full_subtractor_4_1_d1),
    .D0(both_plus_or_both_minus_c1), .S1(S1_out), .S0(S0_out), .Y(R1));
  selector_4_1 selector_4_1_3 (
    .D3(full_subtractor_4_3_d2), .D2(full_subtractor_4_2_d2), .D1(full_subtractor_4_1_d2),
    .D0(both_plus_or_both_minus_c2), .S1(S1_out), .S0(S0_out), .Y(R2));
  selector_4_1 selector_4_1_4 (
    .D3(sign2_out), .D2(1'b0), .D1(sign1_out), .D0(both_plus_or_both_minus_co), .S1(S1_out), .S0(S0_out),
    .Y(R3));
endmodule

module comparator_2_3 (
  input  A1,
  input  A0,
  input  B1,
  input  B0,
  output Y_bigger,
  output Y_equal,
  output Y_smaller
);

  wire and_1_out, and_2_out, and_3_out, and_4_out, and_5_out, and_6_out, and_7_out, and_8_out, and_9_out,
       and_10_out, not_1_out, not_2_out, not_3_out, not_4_out;

  not not_1 (not_1_out, A1);
  not not_2 (not_2_out, A0);
  not not_3 (not_3_out, B1);
  not not_4 (not_4_out, B0);
  and and_1 (and_1_out, not_4_out, A0, A1);
  and and_2 (and_2_out, not_3_out, A1);
  and and_3 (and_3_out, not_4_out, not_3_out, A0);
  and and_4 (and_4_out, not_1_out, not_2_out, not_3_out, not_4_out);
  and and_5 (and_5_out, not_1_out, A0, not_3_out, B0);
  and and_6 (and_6_out, A1, not_2_out, B1, not_4_out);
  and and_7 (and_7_out, A1, A0, B1, B0);
  and and_8 (and_8_out, not_1_out, not_2_out, B0);
  and and_9 (and_9_out, not_1_out, B1);
  and and_10 (and_10_out, not_2_out, B1, B0);
  or or_1 (Y_bigger, and_1_out, and_2_out, and_3_out);
  or or_2 (Y_equal, and_4_out, and_5_out, and_6_out, and_7_out);
  or or_3 (Y_smaller, and_8_out, and_9_out, and_10_out);
endmodule

module comparator_4_3 (
  input  A3,
  input  A2,
  input  B3,
  input  B2,
  input  A1,
  input  A0,
  input  B1,
  input  B0,
  output Y_bigger,
  output Y_equal,
  output Y_smaller
);

  wire and_1_out, and_3_out, comparator_2_3_1_y_bigger, comparator_2_3_1_y_equal, comparator_2_3_1_y_smaller,
       comparator_2_3_2_y_bigger, comparator_2_3_2_y_equal, comparator_2_3_2_y_smaller;

  comparator_2_3 comparator_2_3_1 (
    .A1(A3), .A0(A2), .B1(B3), .B0(B2), .Y_bigger(comparator_2_3_1_y_bigger),
    .Y_equal(comparator_2_3_1_y_equal), .Y_smaller(comparator_2_3_1_y_smaller));
  comparator_2_3 comparator_2_3_2 (
    .A1(A1), .A0(A0), .B1(B1), .B0(B0), .Y_bigger(comparator_2_3_2_y_bigger),
    .Y_equal(comparator_2_3_2_y_equal), .Y_smaller(comparator_2_3_2_y_smaller));
  and and_1 (and_1_out, comparator_2_3_1_y_equal, comparator_2_3_2_y_bigger);
  and and_2 (Y_equal, comparator_2_3_1_y_equal, comparator_2_3_2_y_equal);
  and and_3 (and_3_out, comparator_2_3_1_y_equal, comparator_2_3_2_y_smaller);
  or or_1 (Y_bigger, comparator_2_3_1_y_bigger, and_1_out);
  or or_2 (Y_smaller, and_3_out, comparator_2_3_1_y_smaller);
endmodule

module one_s_complement_adder_4 (
  input  in_1,
  input  in_2,
  input  in_3,
  input  in_4,
  input  in_5,
  input  in_6,
  input  in_7,
  input  in_8,
  output out_9,
  output out_10,
  output out_11,
  output out_12
);

  wire sign_magnitude_adder_4_1_r0, sign_magnitude_adder_4_1_r1, sign_magnitude_adder_4_1_r2, xor_1_out,
       xor_2_out, xor_3_out, xor_4_out, xor_5_out, xor_6_out;

  xor xor_1 (xor_1_out, in_1, in_4);
  xor xor_2 (xor_2_out, in_2, in_4);
  xor xor_3 (xor_3_out, in_3, in_4);
  xor xor_4 (xor_4_out, in_5, in_8);
  xor xor_5 (xor_5_out, in_6, in_8);
  xor xor_6 (xor_6_out, in_7, in_8);
  sign_magnitude_adder_4 sign_magnitude_adder_4_1 (
    .A0(xor_1_out), .B0(xor_4_out), .A1(xor_2_out), .B1(xor_5_out), .A2(xor_3_out), .B2(xor_6_out),
    .A3(in_4), .B3(in_8), .R0(sign_magnitude_adder_4_1_r0), .R1(sign_magnitude_adder_4_1_r1),
    .R2(sign_magnitude_adder_4_1_r2), .R3(out_12));
  xor xor_7 (out_9, sign_magnitude_adder_4_1_r0, out_12);
  xor xor_8 (out_10, sign_magnitude_adder_4_1_r1, out_12);
  xor xor_9 (out_11, sign_magnitude_adder_4_1_r2, out_12);
endmodule

module one_s_complement_adder_4_rev (
  input  [3:0] in_1,
  input  [3:0] in_2,
  output [3:0] out_3
);

  wire or_1_out;

  or or_1 (or_1_out, in_2[3], in_1[3]);
  full_adder_4 full_adder_4_1 (
    .A0(in_1[0]), .B0(in_2[0]), .Ci(or_1_out), .A1(in_1[1]), .B1(in_2[1]), .A2(in_1[2]), .B2(in_2[2]),
    .A3(in_1[3]), .B3(in_2[3]), .C0(out_3[0]), .C1(out_3[1]), .C2(out_3[2]), .C3(out_3[3]));  // open: Co
endmodule

module two_s_complement_adder_4_check (
  input  [3:0] A,
  input  Ci,
  input  [3:0] B,
  output [3:0] C,
  output over_flow_check
);

  wire and_1_out, and_2_out, full_adder_4_1_c0, full_adder_4_1_c1, full_adder_4_1_c2, full_adder_4_2_c0,
       full_adder_4_2_c1, full_adder_4_2_c2, full_adder_4_3_c0, full_adder_4_3_c1, full_adder_4_3_c2,
       not_1_out, not_2_out, not_3_out, xor_1_out, xor_2_out, xor_3_out, xor_4_out, xor_5_out, xor_6_out,
       xor_7_out, xor_8_out, xor_9_out;

  not not_1 (not_1_out, A[3]);
  not not_2 (not_2_out, B[3]);
  not not_3 (not_3_out, C[3]);
  xor xor_1 (xor_1_out, A[3], A[0]);
  xor xor_2 (xor_2_out, A[3], A[1]);
  xor xor_3 (xor_3_out, A[3], A[2]);
  xor xor_4 (xor_4_out, B[3], B[0]);
  xor xor_5 (xor_5_out, B[3], B[1]);
  xor xor_6 (xor_6_out, B[3], B[2]);
  and and_1 (and_1_out, not_1_out, not_2_out, C[3]);
  and and_2 (and_2_out, A[3], B[3], not_3_out);
  full_adder_4 full_adder_4_1 (
    .A0(xor_1_out), .B0(1'b0), .Ci(A[3]), .A1(xor_2_out), .B1(1'b0), .A2(xor_3_out), .B2(1'b0), .A3(1'b0),
    .B3(1'b0), .C0(full_adder_4_1_c0), .C1(full_adder_4_1_c1), .C2(full_adder_4_1_c2));  // open: C3, Co
  full_adder_4 full_adder_4_2 (
    .A0(xor_4_out), .B0(1'b0), .Ci(B[3]), .A1(xor_5_out), .B1(1'b0), .A2(xor_6_out), .B2(1'b0), .A3(1'b0),
    .B3(1'b0), .C0(full_adder_4_2_c0), .C1(full_adder_4_2_c1), .C2(full_adder_4_2_c2));  // open: C3, Co
  or or_1 (over_flow_check, and_1_out, and_2_out);
  full_adder_4 full_adder_4_3 (
    .A0(full_adder_4_1_c0), .B0(full_adder_4_2_c0), .Ci(Ci), .A1(full_adder_4_1_c1), .B1(full_adder_4_2_c1),
    .A2(full_adder_4_1_c2), .B2(full_adder_4_2_c2), .A3(A[3]), .B3(B[3]), .C0(full_adder_4_3_c0),
    .C1(full_adder_4_3_c1), .C2(full_adder_4_3_c2), .C3(C[3]));  // open: Co
  xor xor_7 (xor_7_out, C[3], full_adder_4_3_c0);
  xor xor_8 (xor_8_out, C[3], full_adder_4_3_c1);
  xor xor_9 (xor_9_out, C[3], full_adder_4_3_c2);
  full_adder_4 full_adder_4_4 (
    .A0(xor_7_out), .B0(1'b0), .Ci(C[3]), .A1(xor_8_out), .B1(1'b0), .A2(xor_9_out), .B2(1'b0), .A3(1'b0),
    .B3(1'b0), .C0(C[0]), .C1(C[1]), .C2(C[2]));  // open: C3, Co
  LED led_1 (.in(over_flow_check));
endmodule
