// Logisim project F6.circ as structural Verilog: 21 circuits, main circuit workplace_F5
module workplace_F5 (
  input  [7:0] cmd_15,
  input  [7:0] cmd_14,
  input  [7:0] cmd_13,
  input  [7:0] cmd_12,
  input  [7:0] cmd_11,
  input  [7:0] cmd_10,
  input  [7:0] cmd_9,
  input  [7:0] cmd_8,
  input  R,
  input  [7:0] cmd_7,
  input  [7:0] cmd_6,
  input  EN,
  input  [7:0] cmd_5,
  input  [7:0] cmd_4,
  input  [7:0] cmd_3,
  input  [7:0] cmd_2,
  input  [7:0] cmd_1,
  input  [7:0] cmd_0,
  input  [3:0] cmd_max,
  output [7:0] current_cmd,
  output [7:0] output_display
);

  wire and_1_out, and_2_out, clk_out, cmd_bner0_y, cmd_decoder_y0, cmd_decoder_y2, cmd_decoder_y3,
       d_flip_flop_r_1_q, decoder_7_segments_1_sa, decoder_7_segments_1_sb, decoder_7_segments_1_sc,
       decoder_7_segments_1_sd, decoder_7_segments_1_se, decoder_7_segments_1_sf, decoder_7_segments_1_sg,
       decoder_7_segments_1_sh, decoder_7_segments_2_sa, decoder_7_segments_2_sb, decoder_7_segments_2_sc,
       decoder_7_segments_2_sd, decoder_7_segments_2_se, decoder_7_segments_2_sf, decoder_7_segments_2_sg,
       decoder_7_segments_2_sh, not_1_out, not_2_out, not_3_out, or_1_out, write_EN_pre_q;
  wire [1:0] selector_4_1_2bits_1_data, write_addr_pre_q;
  wire [3:0] PC_q;
  wire [7:0] cmd_add_s, GPR_read_data_1, GPR_read_data_2, register_8_1_q, register_8_2_q,
       selector_4_1_8bits_1_y;

  Clock clk (.out(clk_out));
  and and_1 (and_1_out, ~cmd_bner0_y, cmd_decoder_y3);  // AND_Gate
  counter_2_16_tunable_rev PC (
    .D(current_cmd[5:2]), .LD(and_1_out), .clk(clk_out), .R(R), .EN(EN), .max(cmd_max), .Q(PC_q));  // open: C
  or or_1 (or_1_out, cmd_decoder_y2, cmd_decoder_y0);
  D_flip_flop_R_EN write_EN_pre (.D(or_1_out), .clk(clk_out), .R(R), .EN(EN), .Q(write_EN_pre_q));  // open: Qn
  not not_1 (not_1_out, clk_out);
  not not_2 (not_2_out, current_cmd[7]);
  ROM_16_1_8bits cmd (
    .D15(cmd_15), .D14(cmd_14), .D13(cmd_13), .D12(cmd_12), .D11(cmd_11), .D10(cmd_10), .D9(cmd_9),
    .D8(cmd_8), .addr(PC_q), .D7(cmd_7), .D6(cmd_6), .D5(cmd_5), .D4(cmd_4), .D3(cmd_3), .D2(cmd_2),
    .D1(cmd_1), .D0(cmd_0), .data(current_cmd));
  register_8 register_8_1 (.D(selector_4_1_8bits_1_y), .R(R), .clk(clk_out), .EN(write_EN_pre_q), .Q(register_8_1_q));
  RAM_4_1_8bits_rev GPR (
    .write_data(register_8_1_q), .R(R), .clk(not_1_out), .write_EN(write_EN_pre_q),
    .write_addr(write_addr_pre_q), .read_addr_1(selector_4_1_2bits_1_data), .read_addr_2(current_cmd[1:0]),
    .read_data_1(GPR_read_data_1), .read_data_2(GPR_read_data_2));
  register_2 write_addr_pre (.D(current_cmd[5:4]), .R(R), .clk(clk_out), .EN(write_EN_pre_q), .Q(write_addr_pre_q));
  selector_4_1_2bits selector_4_1_2bits_1 (
    .D3(2'b00), .D0(current_cmd[3:2]), .addr(current_cmd[7:6]), .data(selector_4_1_2bits_1_data));  // open: D2, D1
  and and_2 (and_2_out, current_cmd[6], not_2_out);
  full_adder_8 cmd_add (.A(GPR_read_data_1), .B(GPR_read_data_2), .S(cmd_add_s));  // open: Ci, Co
  D_flip_flop_R d_flip_flop_r_1 (.D(and_2_out), .clk(clk_out), .R(R), .Q(d_flip_flop_r_1_q));  // open: Qn
  decoder_2_4 cmd_decoder (
    .A1(current_cmd[7]), .A0(current_cmd[6]), .Y3(cmd_decoder_y3), .Y2(cmd_decoder_y2), .Y0(cmd_decoder_y0));  // open: Y1
  selector_4_1_8bits selector_4_1_8bits_1 (
    .D2({4'b0000, current_cmd[3:0]}), .D0(cmd_add_s), .addr(current_cmd[7:6]), .Y(selector_4_1_8bits_1_y));  // open: D3, D1
  not not_3 (not_3_out, clk_out);
  comparator_8 cmd_bner0 (.A(GPR_read_data_1), .B(GPR_read_data_2), .Y(cmd_bner0_y));
  register_8 register_8_2 (.D(GPR_read_data_2), .R(R), .clk(clk_out), .EN(d_flip_flop_r_1_q), .Q(register_8_2_q));
  register_8 cmd_out (.D(register_8_2_q), .R(R), .clk(not_3_out), .EN(d_flip_flop_r_1_q), .Q(output_display));
  decoder_7_segments decoder_7_segments_1 (
    .I3(output_display[3]), .I2(output_display[2]), .I1(output_display[1]), .I0(output_display[0]),
    .SA(decoder_7_segments_1_sa), .SB(decoder_7_segments_1_sb), .SC(decoder_7_segments_1_sc),
    .SD(decoder_7_segments_1_sd), .SE(decoder_7_segments_1_se), .SF(decoder_7_segments_1_sf),
    .SG(decoder_7_segments_1_sg), .SH(decoder_7_segments_1_sh));
  decoder_7_segments decoder_7_segments_2 (
    .I3(output_display[7]), .I2(output_display[6]), .I1(output_display[5]), .I0(output_display[4]),
    .SA(decoder_7_segments_2_sa), .SB(decoder_7_segments_2_sb), .SC(decoder_7_segments_2_sc),
    .SD(decoder_7_segments_2_sd), .SE(decoder_7_segments_2_se), .SF(decoder_7_segments_2_sf),
    .SG(decoder_7_segments_2_sg), .SH(decoder_7_segments_2_sh));
  _7_Segment_Display u_7_segment_display_1 (
    .g(decoder_7_segments_2_sg), .f(decoder_7_segments_2_sf), .a(decoder_7_segments_2_sa),
    .b(decoder_7_segments_2_sb), .e(decoder_7_segments_2_se), .d(decoder_7_segments_2_sd),
    .c(decoder_7_segments_2_sc), .dp(decoder_7_segments_2_sh));
  _7_Segment_Display u_7_segment_display_2 (
    .g(decoder_7_segments_1_sg), .f(decoder_7_segments_1_sf), .a(decoder_7_segments_1_sa),
    .b(decoder_7_segments_1_sb), .e(decoder_7_segments_1_se), .d(decoder_7_segments_1_sd),
    .c(decoder_7_segments_1_sc), .dp(decoder_7_segments_1_sh));
endmodule

module selector_8_1 (
  input  D7,
  input  D6,
  input  D5,
  input  D4,
  input  D3,
  input  D2,
  input  D1,
  input  D0,
  input  S2,
  input  S1,
  input  S0,
  output Y
);

  wire and_1_out, and_2_out, and_3_out, and_4_out, and_5_out, and_6_out, and_7_out, and_8_out, not_1_out,
       not_2_out, not_3_out, or_1_out, or_2_out;

  not not_1 (not_1_out, S2);
  not not_2 (not_2_out, S1);
  not not_3 (not_3_out, S0);
  and and_1 (and_1_out, not_1_out, not_2_out, not_3_out, D0);
  and and_2 (and_2_out, not_1_out, not_2_out, S0, D1);
  and and_3 (and_3_out, not_1_out, S1, not_3_out, D2);
  and and_4 (and_4_out, not_1_out, S1, S0, D3);
  and and_5 (and_5_out, S2, not_2_out, not_3_out, D4);
  and and_6 (and_6_out, S2, not_2_out, S0, D5);
  and and_7 (and_7_out, S2, S1, not_3_out, D6);
  and and_8 (and_8_out, S2, S1, S0, D7);
  or or_1 (or_1_out, and_1_out, and_2_out, and_3_out, and_4_out);
  or or_2 (or_2_out, and_5_out, and_6_out, and_7_out, and_8_out);
  or or_3 (Y, or_1_out, or_2_out);
endmodule

module ROM_8_1_8bits (
  input  [7:0] D7,
  input  [7:0] D6,
  input  [7:0] D5,
  input  [7:0] D4,
  input  [7:0] D3,
  input  [7:0] D2,
  input  [7:0] D1,
  input  [7:0] D0,
  input  [2:0] addr,
  output [7:0] data
);

  selector_8_1 selector_8_1_1 (
    .D7(D7[7]), .D6(D6[7]), .D5(D5[7]), .D4(D4[7]), .D3(D3[7]), .D2(D2[7]), .D1(D1[7]), .D0(D0[7]),
    .S2(addr[2]), .S1(addr[1]), .S0(addr[0]), .Y(data[7]));
  selector_8_1 selector_8_1_2 (
    .D7(D7[6]), .D6(D6[6]), .D5(D5[6]), .D4(D4[6]), .D3(D3[6]), .D2(D2[6]), .D1(D1[6]), .D0(D0[6]),
    .S2(addr[2]), .S1(addr[1]), .S0(addr[0]), .Y(data[6]));
  selector_8_1 selector_8_1_3 (
    .D7(D7[5]), .D6(D6[5]), .D5(D5[5]), .D4(D4[5]), .D3(D3[5]), .D2(D2[5]), .D1(D1[5]), .D0(D0[5]),
    .S2(addr[2]), .S1(addr[1]), .S0(addr[0]), .Y(data[5]));
  selector_8_1 selector_8_1_4 (
    .D7(D7[4]), .D6(D6[4]), .D5(D5[4]), .D4(D4[4]), .D3(D3[4]), .D2(D2[4]), .D1(D1[4]), .D0(D0[4]),
    .S2(addr[2]), .S1(addr[1]), .S0(addr[0]), .Y(data[4]));
  selector_8_1 selector_8_1_5 (
    .D7(D7[3]), .D6(D6[3]), .D5(D5[3]), .D4(D4[3]), .D3(D3[3]), .D2(D2[3]), .D1(D1[3]), .D0(D0[3]),
    .S2(addr[2]), .S1(addr[1]), .S0(addr[0]), .Y(data[3]));
  selector_8_1 selector_8_1_6 (
    .D7(D7[2]), .D6(D6[2]), .D5(D5[2]), .D4(D4[2]), .D3(D3[2]), .D2(D2[2]), .D1(D1[2]), .D0(D0[2]),
    .S2(addr[2]), .S1(addr[1]), .S0(addr[0]), .Y(data[2]));
  selector_8_1 selector_8_1_7 (
    .D7(D7[1]), .D6(D6[1]), .D5(D5[1]), .D4(D4[1]), .D3(D3[1]), .D2(D2[1]), .D1(D1[1]), .D0(D0[1]),
    .S2(addr[2]), .S1(addr[1]), .S0(addr[0]), .Y(data[1]));
  selector_8_1 selector_8_1_8 (
    .D7(D7[0]), .D6(D6[0]), .D5(D5[0]), .D4(D4[0]), .D3(D3[0]), .D2(D2[0]), .D1(D1[0]), .D0(D0[0]),
    .S2(addr[2]), .S1(addr[1]), .S0(addr[0]), .Y(data[0]));
endmodule

module ROM_16_1_8bits (
  input  [7:0] D15,
  input  [7:0] D14,
  input  [7:0] D13,
  input  [7:0] D12,
  input  [7:0] D11,
  input  [7:0] D10,
  input  [7:0] D9,
  input  [7:0] D8,
  input  [3:0] addr,
  input  [7:0] D7,
  input  [7:0] D6,
  input  [7:0] D5,
  input  [7:0] D4,
  input  [7:0] D3,
  input  [7:0] D2,
  input  [7:0] D1,
  input  [7:0] D0,
  output [7:0] data
);

  wire [7:0] rom_8_1_8bits_1_data, rom_8_1_8bits_2_data;

  ROM_8_1_8bits rom_8_1_8bits_1 (
    .D7(D15), .D6(D14), .D5(D13), .D4(D12), .D3(D11), .D2(D10), .D1(D9), .D0(D8), .addr(addr[2:0]),
    .data(rom_8_1_8bits_1_data));
  ROM_8_1_8bits rom_8_1_8bits_2 (
    .D7(D7), .D6(D6), .D5(D5), .D4(D4), .D3(D3), .D2(D2), .D1(D1), .D0(D0), .addr(addr[2:0]),
    .data(rom_8_1_8bits_2_data));
  selector_2_1 selector_2_1_1 (.D0(rom_8_1_8bits_2_data[7]), .S(addr[3]), .D1(rom_8_1_8bits_1_data[7]), .Y(data[7]));
  selector_2_1 selector_2_1_2 (.D0(rom_8_1_8bits_2_data[6]), .S(addr[3]), .D1(rom_8_1_8bits_1_data[6]), .Y(data[6]));
  selector_2_1 selector_2_1_3 (.D0(rom_8_1_8bits_2_data[5]), .S(addr[3]), .D1(rom_8_1_8bits_1_data[5]), .Y(data[5]));
  selector_2_1 selector_2_1_4 (.D0(rom_8_1_8bits_2_data[4]), .S(addr[3]), .D1(rom_8_1_8bits_1_data[4]), .Y(data[4]));
  selector_2_1 selector_2_1_5 (.D0(rom_8_1_8bits_2_data[3]), .S(addr[3]), .D1(rom_8_1_8bits_1_data[3]), .Y(data[3]));
  selector_2_1 selector_2_1_6 (.D0(rom_8_1_8bits_2_data[2]), .S(addr[3]), .D1(rom_8_1_8bits_1_data[2]), .Y(data[2]));
  selector_2_1 selector_2_1_7 (.D0(rom_8_1_8bits_2_data[1]), .S(addr[3]), .D1(rom_8_1_8bits_1_data[1]), .Y(data[1]));
  selector_2_1 selector_2_1_8 (.D0(rom_8_1_8bits_2_data[0]), .S(addr[3]), .D1(rom_8_1_8bits_1_data[0]), .Y(data[0]));
endmodule

module selector_2_1 (
  input  D0,
  input  S,
  input  D1,
  output Y
);

  wire and_1_out, and_2_out, not_1_out;

  not not_1 (not_1_out, S);
  and and_1 (and_1_out, D0, not_1_out);
  and and_2 (and_2_out, S, D1);
  or or_1 (Y, and_1_out, and_2_out);
endmodule

module selector_4_1 (
  input  D3,
  input  D2,
  input  D1,
  input  D0,
  input  S1,
  input  S0,
  output Y
);

  wire and_1_out, and_2_out, and_3_out, and_4_out, not_1_out, not_2_out;

  not not_1 (not_1_out, S1);
  not not_2 (not_2_out, S0);
  and and_1 (and_1_out, not_1_out, not_2_out, D0);
  and and_2 (and_2_out, not_1_out, S0, D1);
  and and_3 (and_3_out, S1, not_2_out, D2);
  and and_4 (and_4_out, S1, S0, D3);
  or or_1 (Y, and_1_out, and_2_out, and_3_out, and_4_out);
endmodule

module selector_4_1_8bits (
  input  [7:0] D3,
  input  [7:0] D2,
  input  [7:0] D1,
  input  [7:0] D0,
  input  [1:0] addr,
  output [7:0] Y
);

  selector_4_1 selector_4_1_1 (.D3(D3[7]), .D2(D2[7]), .D1(D1[7]), .D0(D0[7]), .S1(addr[1]), .S0(addr[0]), .Y(Y[7]));
  selector_4_1 selector_4_1_2 (.D3(D3[6]), .D2(D2[6]), .D1(D1[6]), .D0(D0[6]), .S1(addr[1]), .S0(addr[0]), .Y(Y[6]));
  selector_4_1 selector_4_1_3 (.D3(D3[5]), .D2(D2[5]), .D1(D1[5]), .D0(D0[5]), .S1(addr[1]), .S0(addr[0]), .Y(Y[5]));
  selector_4_1 selector_4_1_4 (.D3(D3[4]), .D2(D2[4]), .D1(D1[4]), .D0(D0[4]), .S1(addr[1]), .S0(addr[0]), .Y(Y[4]));
  selector_4_1 selector_4_1_5 (.D3(D3[3]), .D2(D2[3]), .D1(D1[3]), .D0(D0[3]), .S1(addr[1]), .S0(addr[0]), .Y(Y[3]));
  selector_4_1 selector_4_1_6 (.D3(D3[2]), .D2(D2[2]), .D1(D1[2]), .D0(D0[2]), .S1(addr[1]), .S0(addr[0]), .Y(Y[2]));
  selector_4_1 selector_4_1_7 (.D3(D3[1]), .D2(D2[1]), .D1(D1[1]), .D0(D0[1]), .S1(addr[1]), .S0(addr[0]), .Y(Y[1]));
  selector_4_1 selector_4_1_8 (.D3(D3[0]), .D2(D2[0]), .D1(D1[0]), .D0(D0[0]), .S1(addr[1]), .S0(addr[0]), .Y(Y[0]));
endmodule

module RAM_4_1_8bits (
  input  [7:0] write_data,
  input  R,
  input  clk,
  input  EN,
  input  [1:0] addr,
  output [7:0] output_data
);

  wire and_1_out, and_2_out, and_3_out, and_4_out, not_1_out, not_2_out;
  wire [7:0] register_8_1_q, register_8_2_q, register_8_3_q, register_8_4_q;

  and and_1 (and_1_out, addr[1], addr[0], EN);
  and and_2 (and_2_out, not_1_out, addr[1], EN);
  and and_3 (and_3_out, addr[0], not_2_out, EN);
  and and_4 (and_4_out, not_2_out, not_1_out, EN);
  not not_1 (not_1_out, addr[0]);
  not not_2 (not_2_out, addr[1]);
  register_8 register_8_1 (.D(write_data), .R(R), .clk(clk), .EN(and_1_out), .Q(register_8_1_q));
  register_8 register_8_2 (.D(write_data), .R(R), .clk(clk), .EN(and_2_out), .Q(register_8_2_q));
  register_8 register_8_3 (.D(write_data), .R(R), .clk(clk), .EN(and_3_out), .Q(register_8_3_q));
  register_8 register_8_4 (.D(write_data), .R(R), .clk(clk), .EN(and_4_out), .Q(register_8_4_q));
  selector_4_1_8bits selector_4_1_8bits_1 (
    .D3(register_8_1_q), .D2(register_8_2_q), .D1(register_8_3_q), .D0(register_8_4_q), .addr(addr),
    .Y(output_data));
endmodule

module decoder_2_4 (
  input  A1,
  input  A0,
  output Y3,
  output Y2,
  output Y1,
  output Y0
);

  wire not_1_out, not_2_out;

  not not_1 (not_1_out, A1);
  not not_2 (not_2_out, A0);
  and and_1 (Y3, A1, A0);
  and and_2 (Y2, A1, not_2_out);
  and and_3 (Y1, not_1_out, A0);
  and and_4 (Y0, not_1_out, not_2_out);
endmodule

module RAM_4_1_8bits_rev (
  input  [7:0] write_data,
  input  R,
  input  clk,
  input  write_EN,
  input  [1:0] write_addr,
  input  [1:0] read_addr_1,
  input  [1:0] read_addr_2,
  output [7:0] read_data_1,
  output [7:0] read_data_2
);

  wire and_1_out, and_2_out, and_3_out, and_4_out, not_1_out, not_2_out;
  wire [7:0] register_8_1_q, register_8_2_q, register_8_3_q, register_8_4_q;

  and and_1 (and_1_out, write_addr[1], write_addr[0], write_EN);
  and and_2 (and_2_out, not_1_out, write_addr[1], write_EN);
  and and_3 (and_3_out, write_addr[0], not_2_out, write_EN);
  and and_4 (and_4_out, not_2_out, not_1_out, write_EN);
  not not_1 (not_1_out, write_addr[0]);
  not not_2 (not_2_out, write_addr[1]);
  register_8 register_8_1 (.D(write_data), .R(R), .clk(clk), .EN(and_1_out), .Q(register_8_1_q));
  register_8 register_8_2 (.D(write_data), .R(R), .clk(clk), .EN(and_2_out), .Q(register_8_2_q));
  register_8 register_8_3 (.D(write_data), .R(R), .clk(clk), .EN(and_3_out), .Q(register_8_3_q));
  register_8 register_8_4 (.D(write_data), .R(R), .clk(clk), .EN(and_4_out), .Q(register_8_4_q));
  selector_4_1_8bits selector_4_1_8bits_1 (
    .D3(register_8_1_q), .D2(register_8_2_q), .D1(register_8_3_q), .D0(register_8_4_q), .addr(read_addr_1),
    .Y(read_data_1));
  selector_4_1_8bits selector_4_1_8bits_2 (
    .D3(register_8_1_q), .D2(register_8_2_q), .D1(register_8_3_q), .D0(register_8_4_q), .addr(read_addr_2),
    .Y(read_data_2));
endmodule

module full_adder_8 (
  input  [7:0] A,
  input  Ci,
  input  [7:0] B,
  output [7:0] S,
  output Co
);

  wire full_adder_1_1_co, full_adder_1_2_co, full_adder_1_3_co, full_adder_1_4_co, full_adder_1_5_co,
       full_adder_1_6_co, full_adder_1_7_co;

  full_adder_1 full_adder_1_1 (.A(A[0]), .B(B[0]), .Ci(Ci), .S(S[0]), .Co(full_adder_1_1_co));
  full_adder_1 full_adder_1_2 (.A(A[1]), .B(B[1]), .Ci(full_adder_1_1_co), .S(S[1]), .Co(full_adder_1_2_co));
  full_adder_1 full_adder_1_3 (.A(A[2]), .B(B[2]), .Ci(full_adder_1_2_co), .S(S[2]), .Co(full_adder_1_3_co));
  full_adder_1 full_adder_1_4 (.A(A[3]), .B(B[3]), .Ci(full_adder_1_3_co), .S(S[3]), .Co(full_adder_1_4_co));
  full_adder_1 full_adder_1_5 (.A(A[4]), .B(B[4]), .Ci(full_adder_1_4_co), .S(S[4]), .Co(full_adder_1_5_co));
  full_adder_1 full_adder_1_6 (.A(A[5]), .B(B[5]), .Ci(full_adder_1_5_co), .S(S[5]), .Co(full_adder_1_6_co));
  full_adder_1 full_adder_1_7 (.A(A[6]), .B(B[6]), .Ci(full_adder_1_6_co), .S(S[6]), .Co(full_adder_1_7_co));
  full_adder_1 full_adder_1_8 (.A(A[7]), .B(B[7]), .Ci(full_adder_1_7_co), .S(S[7]), .Co(Co));
endmodule

module selector_4_1_2bits (
  input  [1:0] D3,
  input  [1:0] D2,
  input  [1:0] D1,
  input  [1:0] D0,
  input  [1:0] addr,
  output [1:0] data
);

  selector_4_1 selector_4_1_1 (.D3(D3[1]), .D2(D2[1]), .D1(D1[1]), .D0(D0[1]), .S1(addr[1]), .S0(addr[0]), .Y(data[1]));
  selector_4_1 selector_4_1_2 (.D3(D3[0]), .D2(D2[0]), .D1(D1[0]), .D0(D0[0]), .S1(addr[1]), .S0(addr[0]), .Y(data[0]));
endmodule

module comparator_8 (
  input  [7:0] A,
  input  [7:0] B,
  output Y
);

  wire xnor_1_out, xnor_2_out, xnor_3_out, xnor_4_out, xnor_5_out, xnor_6_out, xnor_7_out, xnor_8_out;

  xnor xnor_1 (xnor_1_out, A[0], B[0]);
  xnor xnor_2 (xnor_2_out, A[1], B[1]);
  xnor xnor_3 (xnor_3_out, A[2], B[2]);
  xnor xnor_4 (xnor_4_out, A[3], B[3]);
  xnor xnor_5 (xnor_5_out, A[4], B[4]);
  xnor xnor_6 (xnor_6_out, A[5], B[5]);
  xnor xnor_7 (xnor_7_out, A[6], B[6]);
  xnor xnor_8 (xnor_8_out, A[7], B[7]);
  and and_1 (Y, xnor_1_out, xnor_2_out, xnor_3_out, xnor_4_out, xnor_5_out, xnor_6_out, xnor_7_out, xnor_8_out);
endmodule

module workplace_F6 (
  input  [31:0] cmd_0,
  input  [31:0] cmd_1,
  input  [31:0] cmd_2,
  input  [31:0] cmd_3,
  input  [31:0] cmd_4,
  input  [31:0] cmd_5,
  input  [31:0] cmd_6,
  input  [31:0] cmd_7,
  input  [31:0] cmd_8,
  input  [31:0] cmd_9,
  input  [31:0] cmd_10,
  input  [31:0] cmd_11,
  input  [31:0] cmd_12,
  input  [31:0] cmd_13,
  input  [31:0] cmd_14,
  input  [31:0] cmd_15,
  input  clk,
  input  EN,
  input  R,
  input  [3:0] cmd_max,
  output [31:0] current_cmd,
  output [31:0] PC
);

  wire and_1_out, and_2_out, and_3_out, and_4_out, and_5_out, and_6_out, and_7_out, and_8_out, and_9_out,
       and_10_out, comparator_1_eq, comparator_2_eq, comparator_3_eq, comparator_4_eq, comparator_5_eq,
       comparator_6_eq, comparator_7_eq, comparator_8_eq, comparator_9_eq, comparator_10_eq,
       comparator_11_eq, comparator_12_eq, LD_pre_q, not_1_out, not_2_out, not_3_out, not_4_out, or_1_out,
       or_2_out, or_3_out, or_4_out, or_5_out, or_6_out, or_7_out, register_1_q, register_2_q, register_3_q,
       register_4_q, register_5_q, w_EN_pre_q;
  wire [1:0] bitselector_2_out;
  wire [3:0] counter_32bits_rev_1_rom_addr;
  wire [4:0] w_addr_pre_q;
  wire [7:0] bitselector_1_out, multiplexer_9_out;
  wire [31:0] adder_1_out, adder_2_out, adder_3_out, adder_4_out, bit_extender_1_out, bit_extender_2_out,
       bit_extender_3_out, bit_extender_4_out, gpr_1_r_data_1, gpr_1_r_data_2, jalr_target_q,
       multiplexer_2_out, multiplexer_3_out, multiplexer_4_out, multiplexer_5_out, multiplexer_6_out,
       multiplexer_7_out, multiplexer_8_out, ram_1_dout, register_6_q, shifter_1_out, shifter_2_out,
       shifter_3_out, subtractor_1_out, w_data_pre_q;

  or or_1 (or_1_out, or_2_out, and_3_out);
  Register #(.width(1)) w_EN_pre (.D(or_1_out), .en(EN), .clk(clk), .Q(w_EN_pre_q), .clr(R));
  or or_2 (or_2_out, or_3_out, and_2_out, comparator_6_eq);
  Register #(.width(32)) w_data_pre (.D(multiplexer_8_out), .en(EN), .clk(clk), .Q(w_data_pre_q), .clr(R));
  or or_3 (or_3_out, and_5_out, and_4_out, and_6_out);
  Register #(.width(1)) LD_pre (.D(and_6_out), .en(EN), .clk(clk), .Q(LD_pre_q), .clr(R));
  counter_32bits_rev counter_32bits_rev_1 (
    .LD(LD_pre_q), .D(jalr_target_q), .clk(clk), .EN(EN), .R(R), .cmd_max(cmd_max), .PC(PC),
    .ROM_addr(counter_32bits_rev_1_rom_addr));
  Register #(.width(5)) w_addr_pre (.D(current_cmd[11:7]), .en(EN), .clk(clk), .Q(w_addr_pre_q), .clr(R));
  not not_1 (not_1_out, clk);
  Multiplexer #(.select(4), .width(32)) multiplexer_1 (
    .in0(cmd_0), .in1(cmd_1), .in2(cmd_2), .in3(cmd_3), .in4(cmd_4), .in5(cmd_5), .in6(cmd_6), .in7(cmd_7),
    .in8(cmd_8), .in9(cmd_9), .in10(cmd_10), .in11(cmd_11), .in12(cmd_12), .in13(cmd_13), .in14(cmd_14),
    .in15(cmd_15), .out(current_cmd), .sel(counter_32bits_rev_1_rom_addr));
  GPR gpr_1 (
    .clk(not_1_out), .w_data(w_data_pre_q), .w_EN(w_EN_pre_q), .R(R), .w_addr(w_addr_pre_q),
    .r_addr_1(current_cmd[19:15]), .r_addr_2(current_cmd[24:20]), .r_data_1(gpr_1_r_data_1),
    .r_data_2(gpr_1_r_data_2));
  assign bit_extender_1_out = {{12{1'b0}}, current_cmd[31:12]};  // Bit_Extender bit_extender_1
  Adder #(.width(32)) adder_1 (.a(PC), .b(32'h4), .out(adder_1_out));  // open: cin, cout
  Comparator #(.width(3)) comparator_1 (.a(3'b000), .b(current_cmd[14:12]), .eq(comparator_1_eq));  // open: gt, lt
  Comparator #(.width(7)) comparator_2 (.a(7'b0100011), .b(current_cmd[6:0]), .eq(comparator_2_eq));  // open: gt, lt
  Comparator #(.width(3)) comparator_3 (.a(3'b010), .b(current_cmd[14:12]), .eq(comparator_3_eq));  // open: gt, lt
  Comparator #(.width(7)) comparator_4 (.a(7'b0000011), .b(current_cmd[6:0]), .eq(comparator_4_eq));  // open: gt, lt
  Comparator #(.width(3)) comparator_5 (.a(3'b100), .b(current_cmd[14:12]), .eq(comparator_5_eq));  // open: gt, lt
  Comparator #(.width(7)) comparator_6 (.a(7'b0110111), .b(current_cmd[6:0]), .eq(comparator_6_eq));  // open: gt, lt
  Comparator #(.width(7)) comparator_7 (.a(7'b0110011), .b(current_cmd[6:0]), .eq(comparator_7_eq));  // open: gt, lt
  Comparator #(.width(3)) comparator_8 (.a(3'b000), .b(current_cmd[14:12]), .eq(comparator_8_eq));  // open: gt, lt
  Comparator #(.width(7)) comparator_9 (.a({7{1'b0}}), .b(current_cmd[31:25]), .eq(comparator_9_eq));  // open: gt, lt
  Comparator #(.width(7)) comparator_10 (.a(7'b0010011), .b(current_cmd[6:0]), .eq(comparator_10_eq));  // open: gt, lt
  Comparator #(.width(3)) comparator_11 (.a(3'b000), .b(current_cmd[14:12]), .eq(comparator_11_eq));  // open: gt, lt
  Comparator #(.width(7)) comparator_12 (.a(7'b1100111), .b(current_cmd[6:0]), .eq(comparator_12_eq));  // open: gt, lt
  assign bit_extender_2_out = {{20{current_cmd[31]}}, current_cmd[31:20]};  // Bit_Extender bit_extender_2
  Multiplexer #(.width(32)) multiplexer_2 (
    .in0(adder_2_out), .in1(adder_1_out), .out(multiplexer_2_out), .sel(and_6_out));
  and and_1 (and_1_out, comparator_1_eq, comparator_2_eq);
  and and_2 (and_2_out, comparator_3_eq, comparator_4_eq);
  and and_3 (and_3_out, comparator_4_eq, comparator_5_eq);
  and and_4 (and_4_out, comparator_7_eq, comparator_8_eq, comparator_9_eq);
  and and_5 (and_5_out, comparator_10_eq, comparator_11_eq);
  and and_6 (and_6_out, comparator_11_eq, comparator_12_eq);
  Adder #(.width(32)) adder_2 (.a(bit_extender_2_out), .b(gpr_1_r_data_1), .out(adder_2_out));  // open: cin, cout
  Adder #(.width(32)) adder_3 (.a(gpr_1_r_data_1), .b(gpr_1_r_data_2), .out(adder_3_out));  // open: cin, cout
  assign bit_extender_3_out = {{20{current_cmd[31]}}, {current_cmd[31:25], current_cmd[11:7]}};  // Bit_Extender bit_extender_3
  Shifter #(.width(32)) shifter_1 (.in(bit_extender_1_out), .\dist (5'b01100), .out(shifter_1_out));
  Multiplexer #(.width(32)) multiplexer_3 (
    .in0(multiplexer_2_out), .in1(adder_3_out), .out(multiplexer_3_out), .sel(and_4_out));
  Register #(.width(32)) jalr_target (.D({adder_2_out[31:1], 1'b0}), .en(EN), .clk(clk), .Q(jalr_target_q), .clr(R));
  Adder #(.width(32)) adder_4 (.a(gpr_1_r_data_1), .b(bit_extender_3_out), .out(adder_4_out));  // open: cin, cout
  Multiplexer #(.width(32)) multiplexer_4 (
    .in0(multiplexer_3_out), .in1(shifter_1_out), .out(multiplexer_4_out), .sel(comparator_6_eq));
  Register #(.width(1)) register_1 (.D(comparator_2_eq), .en(EN), .clk(clk), .Q(register_1_q), .clr(R));
  not not_2 (not_2_out, bitselector_2_out[1]);
  not not_3 (not_3_out, bitselector_2_out[0]);
  Multiplexer #(.width(32)) multiplexer_5 (
    .in0(adder_2_out), .in1(adder_4_out), .out(multiplexer_5_out), .sel(comparator_2_eq));
  Multiplexer #(.width(32)) multiplexer_6 (
    .in0(multiplexer_4_out), .in1(ram_1_dout), .out(multiplexer_6_out), .sel(and_2_out));
  and and_7 (and_7_out, not_3_out, not_2_out);
  and and_8 (and_8_out, bitselector_2_out[0], not_2_out);
  and and_9 (and_9_out, bitselector_2_out[1], not_3_out);
  and and_10 (and_10_out, bitselector_2_out[1], bitselector_2_out[0]);
  or or_4 (or_4_out, and_7_out, current_cmd[13]);
  or or_5 (or_5_out, and_8_out, current_cmd[13]);
  or or_6 (or_6_out, and_9_out, current_cmd[13]);
  or or_7 (or_7_out, and_10_out, current_cmd[13]);
  Register #(.width(1)) register_2 (.D(or_4_out), .en(EN), .clk(clk), .Q(register_2_q), .clr(R));
  Register #(.width(1)) register_3 (.D(or_5_out), .en(EN), .clk(clk), .Q(register_3_q), .clr(R));
  Register #(.width(1)) register_4 (.D(or_6_out), .en(EN), .clk(clk), .Q(register_4_q), .clr(R));
  Register #(.width(1)) register_5 (.D(or_7_out), .en(EN), .clk(clk), .Q(register_5_q), .clr(R));
  Shifter #(.shift("lr"), .width(32)) shifter_2 (.in(multiplexer_5_out), .\dist (5'b00010), .out(shifter_2_out));
  Multiplexer #(.width(32)) multiplexer_7 (
    .in0(gpr_1_r_data_2),
    .in1({gpr_1_r_data_2[7:0], gpr_1_r_data_2[7:0], gpr_1_r_data_2[7:0], gpr_1_r_data_2[7:0]}),
    .out(multiplexer_7_out), .sel(and_1_out));
  Multiplexer #(.width(32)) multiplexer_8 (
    .in0(multiplexer_6_out), .in1(bit_extender_4_out), .out(multiplexer_8_out), .sel(and_3_out));
  Register #(.width(32)) register_6 (.D(multiplexer_7_out), .en(EN), .clk(clk), .Q(register_6_q), .clr(R));
  not not_4 (not_4_out, clk);
  BitSelector #(.group(8), .width(32)) bitselector_1 (.in(shifter_2_out), .out(bitselector_1_out), .sel(2'b00));
  RAM #(.asyncread("true"), .byteenables("byteEnables"), .dataWidth(32), .\type ("nonvolatile")) ram_1 (
    .addr(bitselector_1_out), .we(register_1_q), .oe(1'b1), .clk(not_4_out), .din(register_6_q),
    .dout(ram_1_dout), .be3(register_5_q), .be2(register_4_q), .be1(register_3_q), .be0(register_2_q));
  Shifter #(.width(32)) shifter_3 (.in(shifter_2_out), .\dist (5'b00010), .out(shifter_3_out));
  Subtractor #(.width(32)) subtractor_1 (
    .a(multiplexer_5_out), .b(shifter_3_out), .out(subtractor_1_out));  // open: bin, bout
  BitSelector #(.group(2), .width(32)) bitselector_2 (.in(subtractor_1_out), .out(bitselector_2_out), .sel(4'b0000));
  Multiplexer #(.select(2), .width(8)) multiplexer_9 (
    .in0(ram_1_dout[7:0]), .in1(ram_1_dout[15:8]), .in2(ram_1_dout[23:16]), .in3(ram_1_dout[31:24]),
    .out(multiplexer_9_out), .sel(bitselector_2_out));
  assign bit_extender_4_out = {{24{1'b0}}, multiplexer_9_out};  // Bit_Extender bit_extender_4

  // Notes on the sheet:
  //   imm_31_12
  //   rd
  //   rs1
  //   rs2
  //   jalr_pc_4
  //   imm_11_0
  //   cmd_lui
  //   cmd_lw
  //   cmd_lbu
  //   cmd_add
  //   cmd_addi
  //   cmd_jalr
  //   addi
  //   add
  //   lw
  //   s1
  //   b0
  //   b1
  //   b2
  //   b3
endmodule

module counter_32bits_rev (
  input  LD,
  input  [31:0] D,
  input  clk,
  input  EN,
  input  R,
  input  [3:0] cmd_max,
  output [31:0] PC,
  output [3:0] ROM_addr
);

  wire comparator_1_eq, not_1_out, or_1_out, register_2_q;
  wire [31:0] adder_1_out, multiplexer_1_out;
  wire [31:4] shifter_1_out;

  not not_1 (not_1_out, clk);
  Register #(.width(32)) register_1 (.D(multiplexer_1_out), .en(EN), .clk(not_1_out), .Q(PC), .clr(or_1_out));
  or or_1 (or_1_out, R, register_2_q);
  Multiplexer #(.width(32)) multiplexer_1 (.in0(adder_1_out), .in1(D), .out(multiplexer_1_out), .sel(LD));
  Comparator #(.width(4)) comparator_1 (.a(cmd_max), .b(ROM_addr), .eq(comparator_1_eq));  // open: gt, lt
  Register #(.width(1)) register_2 (.D(comparator_1_eq), .en(EN), .clk(not_1_out), .Q(register_2_q), .clr(or_1_out));
  Adder #(.width(32)) adder_1 (.a(PC), .b(32'h4), .out(adder_1_out));  // open: cin, cout
  Shifter #(.shift("lr"), .width(32)) shifter_1 (.in(PC), .\dist (5'b00010), .out({shifter_1_out, ROM_addr}));
endmodule

module GPR (
  input  clk,
  input  [31:0] w_data,
  input  w_EN,
  input  R,
  input  [4:0] w_addr,
  input  [4:0] r_addr_1,
  input  [4:0] r_addr_2,
  output [31:0] r_data_1,
  output [31:0] r_data_2
);

  wire decoder_1_out0, decoder_1_out1, decoder_1_out2, decoder_1_out3, decoder_1_out4, decoder_1_out5,
       decoder_1_out6, decoder_1_out7, decoder_1_out8, decoder_1_out9, decoder_1_out10, decoder_1_out11,
       decoder_1_out12, decoder_1_out13, decoder_1_out14, decoder_1_out15;
  wire [31:0] x0_q, x1_q, x2_q, x3_q, x4_q, x5_q, x6_q, x7_q, x8_q, x9_q, x10_q, x11_q, x12_q, x13_q, x14_q,
       x15_q;

  Decoder #(.select(4)) decoder_1 (
    .out0(decoder_1_out0), .out1(decoder_1_out1), .out2(decoder_1_out2), .out3(decoder_1_out3),
    .out4(decoder_1_out4), .out5(decoder_1_out5), .out6(decoder_1_out6), .out7(decoder_1_out7),
    .out8(decoder_1_out8), .out9(decoder_1_out9), .out10(decoder_1_out10), .out11(decoder_1_out11),
    .out12(decoder_1_out12), .out13(decoder_1_out13), .out14(decoder_1_out14), .out15(decoder_1_out15),
    .sel(w_addr[3:0]), .en(w_EN));
  Register #(.width(32)) x0 (.D(w_data), .en(decoder_1_out0), .clk(clk), .Q(x0_q), .clr(1'b1));
  Register #(.width(32)) x8 (.D(w_data), .en(decoder_1_out8), .clk(clk), .Q(x8_q), .clr(R));
  Register #(.width(32)) x1 (.D(w_data), .en(decoder_1_out1), .clk(clk), .Q(x1_q), .clr(R));
  Register #(.width(32)) x9 (.D(w_data), .en(decoder_1_out9), .clk(clk), .Q(x9_q), .clr(R));
  Register #(.width(32)) x2 (.D(w_data), .en(decoder_1_out2), .clk(clk), .Q(x2_q), .clr(R));
  Register #(.width(32)) x10 (.D(w_data), .en(decoder_1_out10), .clk(clk), .Q(x10_q), .clr(R));
  Register #(.width(32)) x3 (.D(w_data), .en(decoder_1_out3), .clk(clk), .Q(x3_q), .clr(R));
  Register #(.width(32)) x11 (.D(w_data), .en(decoder_1_out11), .clk(clk), .Q(x11_q), .clr(R));
  Register #(.width(32)) x4 (.D(w_data), .en(decoder_1_out4), .clk(clk), .Q(x4_q), .clr(R));
  Register #(.width(32)) x12 (.D(w_data), .en(decoder_1_out12), .clk(clk), .Q(x12_q), .clr(R));
  Register #(.width(32)) x5 (.D(w_data), .en(decoder_1_out5), .clk(clk), .Q(x5_q), .clr(R));
  Register #(.width(32)) x13 (.D(w_data), .en(decoder_1_out13), .clk(clk), .Q(x13_q), .clr(R));
  Register #(.width(32)) x6 (.D(w_data), .en(decoder_1_out6), .clk(clk), .Q(x6_q), .clr(R));
  Register #(.width(32)) x14 (.D(w_data), .en(decoder_1_out14), .clk(clk), .Q(x14_q), .clr(R));
  Register #(.width(32)) x7 (.D(w_data), .en(decoder_1_out7), .clk(clk), .Q(x7_q), .clr(R));
  Register #(.width(32)) x15 (.D(w_data), .en(decoder_1_out15), .clk(clk), .Q(x15_q), .clr(R));
  Multiplexer #(.select(4), .width(32)) multiplexer_1 (
    .in0(x0_q), .in1(x1_q), .in2(x2_q), .in3(x3_q), .in4(x4_q), .in5(x5_q), .in6(x6_q), .in7(x7_q),
    .in8(x8_q), .in9(x9_q), .in10(x10_q), .in11(x11_q), .in12(x12_q), .in13(x13_q), .in14(x14_q),
    .in15(x15_q), .out(r_data_1), .sel(r_addr_1[3:0]));
  Multiplexer #(.select(4), .width(32)) multiplexer_2 (
    .in0(x0_q), .in1(x1_q), .in2(x2_q), .in3(x3_q), .in4(x4_q), .in5(x5_q), .in6(x6_q), .in7(x7_q),
    .in8(x8_q), .in9(x9_q), .in10(x10_q), .in11(x11_q), .in12(x12_q), .in13(x13_q), .in14(x14_q),
    .in15(x15_q), .out(r_data_2), .sel(r_addr_2[3:0]));
endmodule

module two_s_complement_converter_32_32 (
  input  [31:0] sign_magnitude_two_s_complement,
  output [31:0] two_s_complement_sign_magnitude
);

  wire [30:0] bit_extender_1_out, xor_1_out;

  assign bit_extender_1_out = {{30{sign_magnitude_two_s_complement[31]}}, sign_magnitude_two_s_complement[31]};  // Bit_Extender bit_extender_1
  assign xor_1_out = bit_extender_1_out ^ sign_magnitude_two_s_complement[30:0];  // XOR_Gate xor_1, 31 bits wide
  Adder #(.width(31)) adder_1 (
    .a(xor_1_out), .b({31{1'b0}}), .out(two_s_complement_sign_magnitude[30:0]),
    .cin(sign_magnitude_two_s_complement[31]));  // open: cout

  assign two_s_complement_sign_magnitude[31] = sign_magnitude_two_s_complement[31];
endmodule

module two_s_complement_converter_12_32 (
  input  [11:0] sign_magnitude_two_s_complement,
  output [31:0] two_s_complement_sign_magnitude
);

  wire [10:0] adder_1_out, bit_extender_1_out, xor_1_out;

  assign bit_extender_1_out = {{10{sign_magnitude_two_s_complement[11]}}, sign_magnitude_two_s_complement[11]};  // Bit_Extender bit_extender_1
  assign xor_1_out = bit_extender_1_out ^ sign_magnitude_two_s_complement[10:0];  // XOR_Gate xor_1, 11 bits wide
  Adder #(.width(11)) adder_1 (
    .a(xor_1_out), .b({11{1'b0}}), .out(adder_1_out), .cin(sign_magnitude_two_s_complement[11]));  // open: cout
  assign two_s_complement_sign_magnitude = {{20{sign_magnitude_two_s_complement[11]}}, {sign_magnitude_two_s_complement[11], adder_1_out}};  // Bit_Extender bit_extender_2
endmodule

module minirv (
  input  EN,
  input  R,
  output [31:0] current_cmd,
  output [31:0] PC
);

  wire and_1_out, and_2_out, and_3_out, and_4_out, and_5_out, and_6_out, and_7_out, and_8_out, and_9_out,
       and_10_out, and_11_out, and_12_out, clock_1_out, comparator_1_eq, comparator_2_eq, comparator_3_eq,
       comparator_4_eq, comparator_5_eq, comparator_6_eq, comparator_7_eq, comparator_8_eq, comparator_9_eq,
       comparator_10_eq, comparator_11_eq, comparator_12_eq, LD_pre_q, not_1_out, not_2_out, not_3_out,
       not_4_out, or_1_out, or_2_out, or_3_out, or_4_out, or_5_out, or_6_out, or_7_out, register_1_q,
       register_2_q, register_3_q, register_4_q, register_5_q, register_7_q, rgb_comparator_1_ismem,
       rgb_comparator_1_isvga, w_EN_pre_q;
  wire [1:0] bitselector_2_out;
  wire [4:0] w_addr_pre_q;
  wire [7:0] multiplexer_8_out, rgb_video_1_p4, rgb_video_1_p5;
  wire [19:0] shifter_4_out, shifter_5_out, shifter_6_out, subtractor_2_out;
  wire [23:0] bitselector_1_out, counter_32bits_ex_1_rom_addr, rgb_video_1_p6;
  wire [31:0] adder_1_out, adder_2_out, adder_3_out, adder_4_out, bit_extender_1_out, bit_extender_2_out,
       bit_extender_3_out, bit_extender_4_out, gpr_1_r_data_1, gpr_1_r_data_2, jalr_target_q,
       multiplexer_1_out, multiplexer_2_out, multiplexer_3_out, multiplexer_4_out, multiplexer_5_out,
       multiplexer_6_out, multiplexer_7_out, ram_1_dout, register_6_q, shifter_1_out, shifter_2_out,
       shifter_3_out, subtractor_1_out, w_data_pre_q;

  Clock clock_1 (.out(clock_1_out));
  or or_1 (or_1_out, or_2_out, and_3_out);
  Register #(.width(1)) w_EN_pre (.D(or_1_out), .en(EN), .clk(clock_1_out), .Q(w_EN_pre_q), .clr(R));
  or or_2 (or_2_out, or_3_out, and_2_out, comparator_6_eq);
  Register #(.width(32)) w_data_pre (.D(multiplexer_7_out), .en(EN), .clk(clock_1_out), .Q(w_data_pre_q), .clr(R));
  or or_3 (or_3_out, and_5_out, and_4_out, and_6_out);
  Register #(.width(1)) LD_pre (.D(and_6_out), .en(EN), .clk(clock_1_out), .Q(LD_pre_q), .clr(R));
  ROM #(.addrWidth(24), .dataWidth(32)) rom_1 (.addr(counter_32bits_ex_1_rom_addr), .data(current_cmd));
  counter_32bits_ex counter_32bits_ex_1 (
    .LD(LD_pre_q), .D(jalr_target_q), .clk(clock_1_out), .EN(EN), .R(R), .PC(PC),
    .ROM_addr(counter_32bits_ex_1_rom_addr));
  Register #(.width(5)) w_addr_pre (.D(current_cmd[11:7]), .en(EN), .clk(clock_1_out), .Q(w_addr_pre_q), .clr(R));
  not not_1 (not_1_out, clock_1_out);
  GPR gpr_1 (
    .clk(not_1_out), .w_data(w_data_pre_q), .w_EN(w_EN_pre_q), .R(R), .w_addr(w_addr_pre_q),
    .r_addr_1(current_cmd[19:15]), .r_addr_2(current_cmd[24:20]), .r_data_1(gpr_1_r_data_1),
    .r_data_2(gpr_1_r_data_2));
  assign bit_extender_1_out = {{12{1'b0}}, current_cmd[31:12]};  // Bit_Extender bit_extender_1
  Adder #(.width(32)) adder_1 (.a(PC), .b(32'h4), .out(adder_1_out));  // open: cin, cout
  Comparator #(.width(3)) comparator_1 (.a(3'b000), .b(current_cmd[14:12]), .eq(comparator_1_eq));  // open: gt, lt
  Comparator #(.width(7)) comparator_2 (.a(7'b0100011), .b(current_cmd[6:0]), .eq(comparator_2_eq));  // open: gt, lt
  Comparator #(.width(3)) comparator_3 (.a(3'b010), .b(current_cmd[14:12]), .eq(comparator_3_eq));  // open: gt, lt
  Comparator #(.width(7)) comparator_4 (.a(7'b0000011), .b(current_cmd[6:0]), .eq(comparator_4_eq));  // open: gt, lt
  Comparator #(.width(3)) comparator_5 (.a(3'b100), .b(current_cmd[14:12]), .eq(comparator_5_eq));  // open: gt, lt
  Comparator #(.width(7)) comparator_6 (.a(7'b0110111), .b(current_cmd[6:0]), .eq(comparator_6_eq));  // open: gt, lt
  Comparator #(.width(7)) comparator_7 (.a(7'b0110011), .b(current_cmd[6:0]), .eq(comparator_7_eq));  // open: gt, lt
  Comparator #(.width(3)) comparator_8 (.a(3'b000), .b(current_cmd[14:12]), .eq(comparator_8_eq));  // open: gt, lt
  Comparator #(.width(7)) comparator_9 (.a({7{1'b0}}), .b(current_cmd[31:25]), .eq(comparator_9_eq));  // open: gt, lt
  Comparator #(.width(7)) comparator_10 (.a(7'b0010011), .b(current_cmd[6:0]), .eq(comparator_10_eq));  // open: gt, lt
  Comparator #(.width(3)) comparator_11 (.a(3'b000), .b(current_cmd[14:12]), .eq(comparator_11_eq));  // open: gt, lt
  Comparator #(.width(7)) comparator_12 (.a(7'b1100111), .b(current_cmd[6:0]), .eq(comparator_12_eq));  // open: gt, lt
  assign bit_extender_2_out = {{20{current_cmd[31]}}, current_cmd[31:20]};  // Bit_Extender bit_extender_2
  Multiplexer #(.width(32)) multiplexer_1 (
    .in0(adder_2_out), .in1(adder_1_out), .out(multiplexer_1_out), .sel(and_6_out));
  and and_1 (and_1_out, comparator_1_eq, comparator_2_eq);
  and and_2 (and_2_out, comparator_3_eq, comparator_4_eq);
  and and_3 (and_3_out, comparator_4_eq, comparator_5_eq);
  and and_4 (and_4_out, comparator_7_eq, comparator_8_eq, comparator_9_eq);
  and and_5 (and_5_out, comparator_10_eq, comparator_11_eq);
  and and_6 (and_6_out, comparator_11_eq, comparator_12_eq);
  Adder #(.width(32)) adder_2 (.a(bit_extender_2_out), .b(gpr_1_r_data_1), .out(adder_2_out));  // open: cin, cout
  Adder #(.width(32)) adder_3 (.a(gpr_1_r_data_1), .b(gpr_1_r_data_2), .out(adder_3_out));  // open: cin, cout
  assign bit_extender_3_out = {{20{current_cmd[31]}}, {current_cmd[31:25], current_cmd[11:7]}};  // Bit_Extender bit_extender_3
  Shifter #(.width(32)) shifter_1 (.in(bit_extender_1_out), .\dist (5'b01100), .out(shifter_1_out));
  Multiplexer #(.width(32)) multiplexer_2 (
    .in0(multiplexer_1_out), .in1(adder_3_out), .out(multiplexer_2_out), .sel(and_4_out));
  Register #(.width(32)) jalr_target (
    .D({adder_2_out[31:1], 1'b0}), .en(EN), .clk(clock_1_out), .Q(jalr_target_q), .clr(R));
  Adder #(.width(32)) adder_4 (.a(gpr_1_r_data_1), .b(bit_extender_3_out), .out(adder_4_out));  // open: cin, cout
  and and_7 (and_7_out, rgb_comparator_1_ismem, comparator_2_eq);
  Multiplexer #(.width(32)) multiplexer_3 (
    .in0(multiplexer_2_out), .in1(shifter_1_out), .out(multiplexer_3_out), .sel(comparator_6_eq));
  Register #(.width(1)) register_1 (.D(and_7_out), .en(EN), .clk(clock_1_out), .Q(register_1_q), .clr(R));
  not not_2 (not_2_out, bitselector_2_out[1]);
  not not_3 (not_3_out, bitselector_2_out[0]);
  Multiplexer #(.width(32)) multiplexer_4 (
    .in0(adder_2_out), .in1(adder_4_out), .out(multiplexer_4_out), .sel(comparator_2_eq));
  Multiplexer #(.width(32)) multiplexer_5 (
    .in0(multiplexer_3_out), .in1(ram_1_dout), .out(multiplexer_5_out), .sel(and_2_out));
  and and_8 (and_8_out, not_3_out, not_2_out);
  and and_9 (and_9_out, bitselector_2_out[0], not_2_out);
  and and_10 (and_10_out, bitselector_2_out[1], not_3_out);
  and and_11 (and_11_out, bitselector_2_out[1], bitselector_2_out[0]);
  or or_4 (or_4_out, and_8_out, current_cmd[13]);
  or or_5 (or_5_out, and_9_out, current_cmd[13]);
  or or_6 (or_6_out, and_10_out, current_cmd[13]);
  or or_7 (or_7_out, and_11_out, current_cmd[13]);
  Register #(.width(1)) register_2 (.D(or_4_out), .en(EN), .clk(clock_1_out), .Q(register_2_q), .clr(R));
  Register #(.width(1)) register_3 (.D(or_5_out), .en(EN), .clk(clock_1_out), .Q(register_3_q), .clr(R));
  Register #(.width(1)) register_4 (.D(or_6_out), .en(EN), .clk(clock_1_out), .Q(register_4_q), .clr(R));
  Register #(.width(1)) register_5 (.D(or_7_out), .en(EN), .clk(clock_1_out), .Q(register_5_q), .clr(R));
  Shifter #(.shift("lr"), .width(32)) shifter_2 (.in(multiplexer_4_out), .\dist (5'b00010), .out(shifter_2_out));
  Multiplexer #(.width(32)) multiplexer_6 (
    .in0(gpr_1_r_data_2),
    .in1({gpr_1_r_data_2[7:0], gpr_1_r_data_2[7:0], gpr_1_r_data_2[7:0], gpr_1_r_data_2[7:0]}),
    .out(multiplexer_6_out), .sel(and_1_out));
  Multiplexer #(.width(32)) multiplexer_7 (
    .in0(multiplexer_5_out), .in1(bit_extender_4_out), .out(multiplexer_7_out), .sel(and_3_out));
  Register #(.width(32)) register_6 (.D(multiplexer_6_out), .en(EN), .clk(clock_1_out), .Q(register_6_q), .clr(R));
  not not_4 (not_4_out, clock_1_out);
  BitSelector #(.group(24), .width(32)) bitselector_1 (.in(shifter_2_out), .out(bitselector_1_out), .sel(1'b0));
  Shifter #(.width(32)) shifter_3 (.in(shifter_2_out), .\dist (5'b00010), .out(shifter_3_out));
  RAM #(.addrWidth(24), .asyncread("true"), .byteenables("byteEnables"), .dataWidth(32), .\type ("nonvolatile")) ram_1 (
    .addr(bitselector_1_out), .we(register_1_q), .oe(1'b1), .clk(not_4_out), .din(register_6_q),
    .dout(ram_1_dout), .be3(register_5_q), .be2(register_4_q), .be1(register_3_q), .be0(register_2_q));
  Subtractor #(.width(32)) subtractor_1 (
    .a(multiplexer_4_out), .b(shifter_3_out), .out(subtractor_1_out));  // open: bin, bout
  RGB_comparator rgb_comparator_1 (
    .addr_input(multiplexer_4_out), .isMEM(rgb_comparator_1_ismem), .isVGA(rgb_comparator_1_isvga));
  BitSelector #(.group(2), .width(32)) bitselector_2 (.in(subtractor_1_out), .out(bitselector_2_out), .sel(4'b0000));
  Multiplexer #(.select(2), .width(8)) multiplexer_8 (
    .in0(ram_1_dout[7:0]), .in1(ram_1_dout[15:8]), .in2(ram_1_dout[23:16]), .in3(ram_1_dout[31:24]),
    .out(multiplexer_8_out), .sel(bitselector_2_out));
  and and_12 (and_12_out, comparator_2_eq, rgb_comparator_1_isvga);
  assign bit_extender_4_out = {{24{1'b0}}, multiplexer_8_out};  // Bit_Extender bit_extender_4
  Register #(.width(1)) register_7 (.D(and_12_out), .en(EN), .clk(clock_1_out), .Q(register_7_q), .clr(R));
  // RGB_Video #(.cursor("No Cursor"), .height(256), .scale(1), .width(256)) rgb_video_1: pin names not known; wires that end beside it: R, not_4_out, register_7_q, rgb_video_1_p4, rgb_video_1_p5, rgb_video_1_p6
  Register #(.width(24)) register_8 (.D(gpr_1_r_data_2[23:0]), .en(EN), .clk(clock_1_out), .Q(rgb_video_1_p6), .clr(R));
  Shifter #(.shift("lr"), .width(20)) shifter_4 (.in(multiplexer_4_out[19:0]), .\dist (5'b00010), .out(shifter_4_out));
  BitSelector #(.group(8), .width(20)) bitselector_3 (.in(subtractor_2_out), .out(rgb_video_1_p4), .sel(2'b00));
  BitSelector #(.group(8), .width(20)) bitselector_4 (.in(shifter_5_out), .out(rgb_video_1_p5), .sel(2'b00));
  Shifter #(.shift("lr"), .width(20)) shifter_5 (.in(shifter_4_out), .\dist (5'b01000), .out(shifter_5_out));
  Shifter #(.width(20)) shifter_6 (.in(shifter_5_out), .\dist (5'b01000), .out(shifter_6_out));
  Subtractor #(.width(20)) subtractor_2 (
    .a(shifter_4_out), .b(shifter_6_out), .out(subtractor_2_out));  // open: bin, bout

  // Notes on the sheet:
  //   contents of rom_1 (hex, n*v repeats v):
  //   413 93137 10113 10b7 dbc08093 80e7 fe012823 fea10923 fea12423 fe914203 fe4109a3 ff012783 f787b3
  //   f787b3 4b6b7 f0068693 fdc10113 d787b3 10000713 f12423 10593 100793 b00513 2112023 12023 12223 e12623
  //   e12823 f10a23 10b7 a8408093 80e7 2012083 2410113 8067 ff410113 112423 10b7 a7c08093 80e7 513 1800093
  //   80e7 812083 513 c10113 8067 852583 feb12823 fe812e23 3437 a0840413 ff014183 3401b3 1c183 ff114203
  //   440233 24203 4181b3 ff214203 440233 24203 4181b3 ff314203 440233 24203 4181b3 3237 a0020213 320233
  //   24203 ffc12403 420233 420233 410233 11b7 85c18193 fe312823 14800193 fe312623 fec22203 20067 1052703
  //   52683 452783 fe810113 e12423 112a23 fed12823 fef12623 13737 c0070713 fe012223 ff314203 fe4102a3
  //   fef14203 fe410223 fe412203 470233 24203 fe4105a3 ff214203 fe4102a3 fee14203 fe410223 fe412203 470233
  //   24203 fe410523 ff114203 fe4102a3 fed14203 fe410223 fe412203 470233 24203 fe4104a3 ff014203 fe4102a3
  //   fec14203 fe410223 fe412203 470233 24203 fe410423 fe812703 c52603 fee12823 fe812e23 3437 a0840413
  //   ff014183 3401b3 1c183 ff114203 440233 24203 4181b3 ff214203 440233 24203 4181b3 ff314203 440233
  //   24203 4181b3 3237 a0020213 320233 24203 ffc12403 420233 420233 410233 66800193 fe312823 28000193
  //   fe312623 fec22203 20067 c68733 10000513 fe812e23 fe912c23 fee12823 50413 ff012483 fe812423 feb14183
  //   3181b3 fe312423 fe914183 3181b3 fe912423 feb14203 420233 fe412423 fe914203 4181b3 3181b3 fe312a23
  //   fe912423 33237 b0020213 feb14183 4181b3 1c183 fe3103a3 fea14183 4181b3 1c183 fe310323 fe914183
  //   4181b3 1c183 fe3102a3 fe814183 4181b3 1c183 fe310223 ff412183 fe412203 440233 120213 fe412423
  //   feb14203 420233 fe412423 fe914203 4181b3 3237 b0820213 320233 ff812483 ffc12403 24203 420233 420233
  //   410233 11b7 86018193 fe312823 38800193 fe312623 fec22203 20067 812703 10000513 812823 e78733
  //   fe812e23 fe912c23 fee12823 50413 ff012483 fe812423 feb14183 3181b3 fe312423 fe914183 3181b3 fe912423
  //   feb14203 420233 fe412423 fe914203 4181b3 3181b3 fe312a23 fe912423 33237 b0020213 feb14183 4181b3
  //   1c183 fe3103a3 fea14183 4181b3 1c183 fe310323 fe914183 4181b3 1c183 fe3102a3 fe814183 4181b3 1c183
  //   fe310223 ff412183 fe412203 440233 120213 fe412423 feb14203 420233 fe412423 fe914203 4181b3 3237
  //   b0820213 320233 ff812483 ffc12403 24203 420233 420233 410233 11b7 86418193 fe312823 49800193
  //   fe312623 fec22203 20067 8*f787b3 d787b3 f787b3 f787b3 20000437 f40433 812783 c60633 c60633 fef12423
  //   feb14183 3181b3 fe312423 fe914183 fff78213 fe412423 feb14203 420233 fe412423 fe914203 4181b3 3237
  //   b1820213 418233 24203 420233 420233 410233 65800193 fe312823 53c00193 fe312623 fec22203 20067 912623
  //   493 40513 c12223 b12023 10b7 de008093 80e7 12583 412603 812783 148493 40040413 c585b3 fef12823
  //   fe912623 fe812e23 fe912c23 4b437 d0040413 ff014183 340233 100193 320023 fec14183 3401b3 18023 24183
  //   ff114483 940233 100493 920023 fed14483 9404b3 48023 24483 9181b3 ff214483 940233 100493 920023
  //   fee14483 9404b3 48023 24483 9181b3 ff314483 940233 100493 920023 fef14483 9404b3 48023 24483 9181b3
  //   3237 a0020213 320233 24203 ff812483 ffc12403 420233 420233 410233 65400193 fe312823 54400193
  //   fe312623 fec22203 20067 c12483 1012403 1412083 1810113 8067 10000713 fec12823 fee12623 fe812e23
  //   fe912c23 4b437 d0040413 ff014183 340233 100193 320023 fec14183 3401b3 18023 24183 ff114483 940233
  //   100493 920023 fed14483 9404b3 48023 24483 9181b3 ff214483 940233 100493 920023 fee14483 9404b3 48023
  //   24483 9181b3 ff314483 940233 100493 920023 fef14483 9404b3 48023 24483 9181b3 3237 a0020213 320233
  //   24203 ff812483 ffc12403 420233 420233 410233 74c00193 fe312823 28000193 fe312623 fec22203 20067
  //   812703 fee12823 fec12623 fe812e23 fe912c23 4b437 d0040413 ff014183 340233 100193 320023 fec14183
  //   3401b3 18023 24183 ff114483 940233 100493 920023 fed14483 9404b3 48023 24483 9181b3 ff214483 940233
  //   100493 920023 fee14483 9404b3 48023 24483 9181b3 ff314483 940233 100493 920023 fef14483 9404b3 48023
  //   24483 9181b3 3237 a0020213 320233 24203 ff812483 ffc12403 420233 420233 410233 11b7 83418193
  //   fe312823 38800193 fe312623 fec22203 20067 1412083 40637 20000537 1810113 1237 de020213 20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
  //   imm_31_12
  //   rd
  //   rs1
  //   rs2
  //   jalr_pc_4
  //   imm_11_0
  //   cmd_lui
  //   cmd_sw_sb
  //   cmd_lw
  //   cmd_lbu
  //   cmd_add
  //   cmd_addi
  //   cmd_jalr
  //   addi
  //   add
  //   lw
  //   s1
  //   b0
  //   b1
  //   b2
  //   b3
endmodule

module counter_32bits_ex (
  input  LD,
  input  [31:0] D,
  input  clk,
  input  EN,
  input  R,
  output [31:0] PC,
  output [23:0] ROM_addr
);

  wire comparator_1_eq, not_1_out, or_1_out, register_2_q;
  wire [31:0] adder_1_out, multiplexer_1_out;
  wire [31:24] shifter_1_out;

  not not_1 (not_1_out, clk);
  Register #(.width(32)) register_1 (.D(multiplexer_1_out), .en(EN), .clk(not_1_out), .Q(PC), .clr(or_1_out));
  or or_1 (or_1_out, R, register_2_q);
  Multiplexer #(.width(32)) multiplexer_1 (.in0(adder_1_out), .in1(D), .out(multiplexer_1_out), .sel(LD));
  Comparator #(.width(24)) comparator_1 (.a({24{1'b1}}), .b(ROM_addr), .eq(comparator_1_eq));  // open: gt, lt
  Register #(.width(1)) register_2 (.D(comparator_1_eq), .en(EN), .clk(not_1_out), .Q(register_2_q), .clr(or_1_out));
  Adder #(.width(32)) adder_1 (.a(PC), .b(32'h4), .out(adder_1_out));  // open: cin, cout
  Shifter #(.shift("lr"), .width(32)) shifter_1 (.in(PC), .\dist (5'b00010), .out({shifter_1_out, ROM_addr}));
endmodule

module RGB_comparator (
  input  [31:0] addr_input,
  output isMEM,
  output isVGA
);

  wire and_1_out, and_2_out, and_3_out, and_4_out, and_5_out, comparator_1_eq, comparator_1_gt,
       comparator_1_lt, comparator_2_eq, comparator_2_gt, comparator_2_lt;

  Comparator #(.width(32)) comparator_1 (
    .a(addr_input), .b(32'h20000000), .gt(comparator_1_gt), .eq(comparator_1_eq), .lt(comparator_1_lt));
  Comparator #(.width(32)) comparator_2 (
    .a(addr_input), .b(32'h20040000), .gt(comparator_2_gt), .eq(comparator_2_eq), .lt(comparator_2_lt));
  and and_1 (and_1_out, comparator_2_lt, comparator_1_lt);
  and and_2 (and_2_out, comparator_1_gt, comparator_2_eq);
  and and_3 (and_3_out, comparator_1_gt, comparator_2_gt);
  and and_4 (and_4_out, comparator_1_eq, comparator_2_lt);
  and and_5 (and_5_out, comparator_1_gt, comparator_2_lt);
  or or_1 (isMEM, and_1_out, and_2_out, and_3_out);
  or or_2 (isVGA, and_4_out, and_5_out);
endmodule
